// Logisim project 8bitCPU.circ as structural Verilog
module main (
);

  MEM_8_BIT mem_8_bit_1 ();  // open: in_2, in_1, out_3
endmodule

module Timer555 (
);

  Pull_Resistor pull_resistor_1 ();  // open: node
endmodule

module ActiveLowSRLatch (
  input  S,
  input  R,
  output Q,
  output NQ
);

  nand nand_1 (Q, S, NQ);
  nand nand_2 (NQ, Q, R);
endmodule

module ActiveHighWithEnable (
  input  S,
  input  E,
  input  R,
  output Q,
  output NQ
);

  wire nand_1_out, nand_2_out;

  nand nand_1 (nand_1_out, S, E);
  nand nand_2 (nand_2_out, E, R);
  nand nand_3 (Q, nand_1_out, NQ);
  nand nand_4 (NQ, Q, nand_2_out);
endmodule

module oneBitMemoryCell (
  input  S,
  input  E,
  output Q,
  output NQ
);

  wire nand_1_out, nand_2_out, not_1_out;

  not not_1 (not_1_out, S);
  nand nand_1 (nand_1_out, S, E);
  nand nand_2 (nand_2_out, E, not_1_out);
  nand nand_3 (Q, nand_1_out, NQ);
  nand nand_4 (NQ, Q, nand_2_out);
endmodule

module oneBitSimplified (
  input  S,
  input  E,
  output Q
);

  wire nand_1_out, nand_2_out, nand_4_out;

  nand nand_1 (nand_1_out, S, E);
  nand nand_2 (nand_2_out, nand_1_out, E);
  nand nand_3 (Q, nand_1_out, nand_4_out);
  nand nand_4 (nand_4_out, Q, nand_2_out);
endmodule

module MEM_1_BIT (
  input  S,
  input  E,
  output Q
);

  wire nand_1_out, nand_2_out, nand_4_out;

  nand nand_1 (nand_1_out, S, E);
  nand nand_2 (nand_2_out, nand_1_out, E);
  nand nand_3 (Q, nand_1_out, nand_4_out);
  nand nand_4 (nand_4_out, Q, nand_2_out);
endmodule

module MEM_8_BIT (
  input  [7:0] in_1,
  input  in_2,
  output [7:0] out_3
);

  MEM_1_BIT mem_1_bit_1 (.S(in_1[0]), .E(in_2), .Q(out_3[0]));
  MEM_1_BIT mem_1_bit_2 (.S(in_1[1]), .E(in_2), .Q(out_3[1]));
  MEM_1_BIT mem_1_bit_3 (.S(in_1[2]), .E(in_2), .Q(out_3[2]));
  MEM_1_BIT mem_1_bit_4 (.S(in_1[3]), .E(in_2), .Q(out_3[3]));
  MEM_1_BIT mem_1_bit_5 (.S(in_1[4]), .E(in_2), .Q(out_3[4]));
  MEM_1_BIT mem_1_bit_6 (.S(in_1[5]), .E(in_2), .Q(out_3[5]));
  MEM_1_BIT mem_1_bit_7 (.S(in_1[6]), .E(in_2), .Q(out_3[6]));
  MEM_1_BIT mem_1_bit_8 (.S(in_1[7]), .E(in_2), .Q(out_3[7]));
endmodule

module eighBitMemoryCell (
  input  in_1,
  input  in_2,
  input  in_3,
  input  in_4,
  input  in_5,
  input  in_6,
  input  in_7,
  input  in_8,
  input  in_9,
  output Q,
  output Q_2,
  output Q_3,
  output Q_4,
  output Q_5,
  output Q_6,
  output Q_7,
  output Q_8
);

  wire nand_1_out, nand_2_out, nand_3_out, nand_4_out, nand_5_out, nand_6_out, nand_7_out, nand_8_out,
       nand_9_out, nand_10_out, nand_11_out, nand_12_out, nand_13_out, nand_14_out, nand_15_out, nand_16_out,
       nand_18_out, nand_20_out, nand_22_out, nand_24_out, nand_26_out, nand_28_out, nand_30_out, nand_32_out;

  nand nand_1 (nand_1_out, in_2, in_1);
  nand nand_2 (nand_2_out, nand_1_out, in_1);
  nand nand_3 (nand_3_out, in_3, in_1);
  nand nand_4 (nand_4_out, nand_3_out, in_1);
  nand nand_5 (nand_5_out, in_4, in_1);
  nand nand_6 (nand_6_out, nand_5_out, in_1);
  nand nand_7 (nand_7_out, in_5, in_1);
  nand nand_8 (nand_8_out, nand_7_out, in_1);
  nand nand_9 (nand_9_out, in_6, in_1);
  nand nand_10 (nand_10_out, nand_9_out, in_1);
  nand nand_11 (nand_11_out, in_7, in_1);
  nand nand_12 (nand_12_out, nand_11_out, in_1);
  nand nand_13 (nand_13_out, in_8, in_1);
  nand nand_14 (nand_14_out, nand_13_out, in_1);
  nand nand_15 (nand_15_out, in_9, in_1);
  nand nand_16 (nand_16_out, nand_15_out, in_1);
  nand nand_17 (Q, nand_1_out, nand_18_out);
  nand nand_18 (nand_18_out, Q, nand_2_out);
  nand nand_19 (Q_2, nand_3_out, nand_20_out);
  nand nand_20 (nand_20_out, Q_2, nand_4_out);
  nand nand_21 (Q_3, nand_5_out, nand_22_out);
  nand nand_22 (nand_22_out, Q_3, nand_6_out);
  nand nand_23 (Q_4, nand_7_out, nand_24_out);
  nand nand_24 (nand_24_out, Q_4, nand_8_out);
  nand nand_25 (Q_5, nand_9_out, nand_26_out);
  nand nand_26 (nand_26_out, Q_5, nand_10_out);
  nand nand_27 (Q_6, nand_11_out, nand_28_out);
  nand nand_28 (nand_28_out, Q_6, nand_12_out);
  nand nand_29 (Q_7, nand_13_out, nand_30_out);
  nand nand_30 (nand_30_out, Q_7, nand_14_out);
  nand nand_31 (Q_8, nand_15_out, nand_32_out);
  nand nand_32 (nand_32_out, Q_8, nand_16_out);

  // Notes on the sheet:
  //   S
  //   E
  //   S
  //   E
  //   S
  //   E
  //   S
  //   E
  //   S
  //   E
  //   S
  //   E
  //   S
  //   E
  //   S
  //   E
endmodule

module REG_8_BIT (
  input  [7:0] in_1,
  input  in_2,
  output [7:0] out_3
);

  and and_1 (out_3[0], in_1[0], in_2);
  and and_2 (out_3[1], in_1[1], in_2);
  and and_3 (out_3[2], in_1[2], in_2);
  and and_4 (out_3[3], in_1[3], in_2);
  and and_5 (out_3[4], in_1[4], in_2);
  and and_6 (out_3[5], in_1[5], in_2);
  and and_7 (out_3[6], in_1[6], in_2);
  and and_8 (out_3[7], in_1[7], in_2);
endmodule
