// Logisim project 8bitCPU_Scratch.circ as structural Verilog
module ActiveLowSRLatch (
  input  S,
  input  R,
  output Q,
  output NQ
);

  nand nand_1 (Q, S, NQ);
  nand nand_2 (NQ, Q, R);
endmodule

module ActiveHighWithEnable (
  input  S,
  input  E,
  input  R,
  output Q,
  output NQ
);

  wire nand_1_out, nand_2_out;

  nand nand_1 (nand_1_out, S, E);
  nand nand_2 (nand_2_out, E, R);
  nand nand_3 (Q, nand_1_out, NQ);
  nand nand_4 (NQ, Q, nand_2_out);
endmodule

module oneBitMemoryCell (
  input  S,
  input  E,
  output Q,
  output NQ
);

  wire nand_1_out, nand_2_out, not_1_out;

  not not_1 (not_1_out, S);
  nand nand_1 (nand_1_out, S, E);
  nand nand_2 (nand_2_out, E, not_1_out);
  nand nand_3 (Q, nand_1_out, NQ);
  nand nand_4 (NQ, Q, nand_2_out);
endmodule

module oneBitSimplified (
  input  S,
  input  E,
  output Q
);

  wire nand_1_out, nand_2_out, nand_4_out;

  nand nand_1 (nand_1_out, S, E);
  nand nand_2 (nand_2_out, nand_1_out, E);
  nand nand_3 (Q, nand_1_out, nand_4_out);
  nand nand_4 (nand_4_out, Q, nand_2_out);
endmodule

module MEM_1_BIT (
  input  S,
  input  E,
  output Q
);

  wire nand_1_out, nand_2_out, nand_4_out;

  nand nand_1 (nand_1_out, S, E);
  nand nand_2 (nand_2_out, nand_1_out, E);
  nand nand_3 (Q, nand_1_out, nand_4_out);
  nand nand_4 (nand_4_out, Q, nand_2_out);
endmodule

module MEM_8_BIT (
  input  [7:0] in_1,
  input  in_2,
  output [7:0] out_3
);

  MEM_1_BIT mem_1_bit_1 (.S(in_1[0]), .E(in_2), .Q(out_3[0]));
  MEM_1_BIT mem_1_bit_2 (.S(in_1[1]), .E(in_2), .Q(out_3[1]));
  MEM_1_BIT mem_1_bit_3 (.S(in_1[2]), .E(in_2), .Q(out_3[2]));
  MEM_1_BIT mem_1_bit_4 (.S(in_1[3]), .E(in_2), .Q(out_3[3]));
  MEM_1_BIT mem_1_bit_5 (.S(in_1[4]), .E(in_2), .Q(out_3[4]));
  MEM_1_BIT mem_1_bit_6 (.S(in_1[5]), .E(in_2), .Q(out_3[5]));
  MEM_1_BIT mem_1_bit_7 (.S(in_1[6]), .E(in_2), .Q(out_3[6]));
  MEM_1_BIT mem_1_bit_8 (.S(in_1[7]), .E(in_2), .Q(out_3[7]));
endmodule

module eighBitMemoryCell (
  input  in_1,
  input  in_2,
  input  in_3,
  input  in_4,
  input  in_5,
  input  in_6,
  input  in_7,
  input  in_8,
  input  in_9,
  output Q,
  output Q_2,
  output Q_3,
  output Q_4,
  output Q_5,
  output Q_6,
  output Q_7,
  output Q_8
);

  wire nand_1_out, nand_2_out, nand_3_out, nand_4_out, nand_5_out, nand_6_out, nand_7_out, nand_8_out,
       nand_9_out, nand_10_out, nand_11_out, nand_12_out, nand_13_out, nand_14_out, nand_15_out, nand_16_out,
       nand_18_out, nand_20_out, nand_22_out, nand_24_out, nand_26_out, nand_28_out, nand_30_out, nand_32_out;

  nand nand_1 (nand_1_out, in_2, in_1);
  nand nand_2 (nand_2_out, nand_1_out, in_1);
  nand nand_3 (nand_3_out, in_3, in_1);
  nand nand_4 (nand_4_out, nand_3_out, in_1);
  nand nand_5 (nand_5_out, in_4, in_1);
  nand nand_6 (nand_6_out, nand_5_out, in_1);
  nand nand_7 (nand_7_out, in_5, in_1);
  nand nand_8 (nand_8_out, nand_7_out, in_1);
  nand nand_9 (nand_9_out, in_6, in_1);
  nand nand_10 (nand_10_out, nand_9_out, in_1);
  nand nand_11 (nand_11_out, in_7, in_1);
  nand nand_12 (nand_12_out, nand_11_out, in_1);
  nand nand_13 (nand_13_out, in_8, in_1);
  nand nand_14 (nand_14_out, nand_13_out, in_1);
  nand nand_15 (nand_15_out, in_9, in_1);
  nand nand_16 (nand_16_out, nand_15_out, in_1);
  nand nand_17 (Q, nand_1_out, nand_18_out);
  nand nand_18 (nand_18_out, Q, nand_2_out);
  nand nand_19 (Q_2, nand_3_out, nand_20_out);
  nand nand_20 (nand_20_out, Q_2, nand_4_out);
  nand nand_21 (Q_3, nand_5_out, nand_22_out);
  nand nand_22 (nand_22_out, Q_3, nand_6_out);
  nand nand_23 (Q_4, nand_7_out, nand_24_out);
  nand nand_24 (nand_24_out, Q_4, nand_8_out);
  nand nand_25 (Q_5, nand_9_out, nand_26_out);
  nand nand_26 (nand_26_out, Q_5, nand_10_out);
  nand nand_27 (Q_6, nand_11_out, nand_28_out);
  nand nand_28 (nand_28_out, Q_6, nand_12_out);
  nand nand_29 (Q_7, nand_13_out, nand_30_out);
  nand nand_30 (nand_30_out, Q_7, nand_14_out);
  nand nand_31 (Q_8, nand_15_out, nand_32_out);
  nand nand_32 (nand_32_out, Q_8, nand_16_out);

  // Notes on the sheet:
  //   S
  //   E
  //   S
  //   E
  //   S
  //   E
  //   S
  //   E
  //   S
  //   E
  //   S
  //   E
  //   S
  //   E
  //   S
  //   E
endmodule

module CPU_ENABLE (
  input  [7:0] in_1,
  input  in_2,
  output [7:0] out_3
);

  and and_1 (out_3[0], in_1[0], in_2);
  and and_2 (out_3[1], in_1[1], in_2);
  and and_3 (out_3[2], in_1[2], in_2);
  and and_4 (out_3[3], in_1[3], in_2);
  and and_5 (out_3[4], in_1[4], in_2);
  and and_6 (out_3[5], in_1[5], in_2);
  and and_7 (out_3[6], in_1[6], in_2);
  and and_8 (out_3[7], in_1[7], in_2);
endmodule

module CPU_8_REG (
  input  [7:0] in_1,
  input  in_2,
  input  in_3,
  output [7:0] out_4
);

  wire [7:0] mem_8_bit_1_out_3;

  MEM_8_BIT mem_8_bit_1 (.in_2(in_2), .in_1(in_1), .out_3(mem_8_bit_1_out_3));
  CPU_ENABLE cpu_enable_1 (.in_2(in_3), .in_1(mem_8_bit_1_out_3), .out_3(out_4));
endmodule

module DECODER_2_4 (
  input  A,
  input  B,
  output out_3,
  output out_4,
  output out_5,
  output out_6
);

  wire not_1_out, not_2_out;

  not not_1 (not_1_out, B);
  not not_2 (not_2_out, A);
  and OO (out_3, not_2_out, not_1_out);
  and OI (out_4, A, not_1_out);
  and IO (out_5, B, not_2_out);
  and II (out_6, B, A);
endmodule

module twoToFourDecoder (
  input  A,
  input  B,
  output out_3,
  output out_4,
  output out_5,
  output out_6
);

  wire not_1_out, not_2_out;

  not not_1 (not_1_out, A);
  not not_2 (not_2_out, B);
  and OO (out_3, not_1_out, not_2_out);
  and OI (out_4, not_1_out, B);
  and IO (out_5, A, not_2_out);
  and II (out_6, B, A);

  // Notes on the sheet:
  //   nA
  //   nB
endmodule

module threeToeight (
  input  a,
  input  b,
  input  c,
  output o1,
  output o2,
  output o3,
  output o4,
  output o5,
  output o6,
  output o7,
  output o8
);

  wire nand_1_out, nand_2_out, nand_3_out, nand_4_out, nand_5_out, nand_6_out, nand_7_out, nand_8_out,
       nand_9_out, nand_10_out, nand_11_out, nand_12_out, nand_13_out, nand_14_out, nand_15_out, nand_16_out,
       nand_17_out, nand_18_out, nand_19_out, nand_20_out, nand_21_out, nand_22_out, nand_23_out,
       nand_24_out, nand_25_out, nand_26_out, nand_27_out, nand_28_out, nand_29_out, nand_30_out,
       nand_31_out, nand_32_out, nand_33_out, nand_34_out, nand_35_out, nand_36_out, nand_37_out,
       nand_38_out, nand_39_out, nand_40_out, nand_41_out, nand_42_out, nand_43_out, nand_44_out,
       nand_45_out, nand_46_out, nand_47_out, nand_48_out, nand_49_out, nand_50_out, nand_51_out,
       nand_52_out, nand_53_out, nand_54_out, nand_55_out, nand_56_out, nand_57_out, nand_58_out,
       nand_59_out, nand_60_out, nand_63_out, nand_64_out, nand_65_out, nand_66_out, nand_67_out,
       nand_68_out, nand_69_out, nand_70_out, nand_71_out, nand_72_out, nand_73_out, nand_74_out;

  nand nand_1 (nand_1_out, a, b);
  nand nand_2 (nand_2_out, a, b);
  nand nand_3 (nand_3_out, a, b);
  nand nand_4 (nand_4_out, a, b);
  nand nand_5 (nand_5_out, 1'b1, b);
  nand nand_6 (nand_6_out, 1'b1, b);
  nand nand_7 (nand_7_out, 1'b1, b);
  nand nand_8 (nand_8_out, 1'b1, b);
  nand nand_9 (nand_9_out, 1'b1, a);
  nand nand_10 (nand_10_out, 1'b1, a);
  nand nand_11 (nand_11_out, 1'b1, a);
  nand nand_12 (nand_12_out, 1'b1, a);
  nand nand_13 (nand_13_out, 1'b1, a);
  nand nand_14 (nand_14_out, 1'b1, b);
  nand nand_15 (nand_15_out, 1'b1, a);
  nand nand_16 (nand_16_out, 1'b1, b);
  nand nand_17 (nand_17_out, 1'b1, a);
  nand nand_18 (nand_18_out, 1'b1, b);
  nand nand_19 (nand_19_out, 1'b1, a);
  nand nand_20 (nand_20_out, 1'b1, b);
  nand nand_21 (nand_21_out, nand_1_out, nand_1_out);
  nand nand_22 (nand_22_out, nand_2_out, nand_2_out);
  nand nand_23 (nand_23_out, nand_3_out, nand_3_out);
  nand nand_24 (nand_24_out, 1'b1, c);
  nand nand_25 (nand_25_out, nand_4_out, nand_4_out);
  nand nand_26 (nand_26_out, 1'b1, c);
  nand nand_27 (nand_27_out, a, nand_5_out);
  nand nand_28 (nand_28_out, a, nand_6_out);
  nand nand_29 (nand_29_out, a, nand_7_out);
  nand nand_30 (nand_30_out, a, nand_8_out);
  nand nand_31 (nand_31_out, nand_9_out, b);
  nand nand_32 (nand_32_out, nand_10_out, b);
  nand nand_33 (nand_33_out, nand_11_out, b);
  nand nand_34 (nand_34_out, nand_12_out, b);
  nand nand_35 (nand_35_out, nand_13_out, nand_14_out);
  nand nand_36 (nand_36_out, nand_15_out, nand_16_out);
  nand nand_37 (nand_37_out, nand_17_out, nand_18_out);
  nand nand_38 (nand_38_out, nand_19_out, nand_20_out);
  nand nand_39 (nand_39_out, nand_21_out, c);
  nand nand_40 (nand_40_out, nand_22_out, c);
  nand nand_41 (nand_41_out, nand_23_out, nand_24_out);
  nand nand_42 (nand_42_out, nand_25_out, nand_26_out);
  nand nand_43 (nand_43_out, nand_27_out, nand_27_out);
  nand nand_44 (nand_44_out, nand_28_out, nand_28_out);
  nand nand_45 (nand_45_out, nand_29_out, nand_29_out);
  nand nand_46 (nand_46_out, 1'b1, c);
  nand nand_47 (nand_47_out, nand_30_out, nand_30_out);
  nand nand_48 (nand_48_out, 1'b1, c);
  nand nand_49 (nand_49_out, nand_31_out, nand_31_out);
  nand nand_50 (nand_50_out, nand_32_out, nand_32_out);
  nand nand_51 (nand_51_out, nand_33_out, nand_33_out);
  nand nand_52 (nand_52_out, 1'b1, c);
  nand nand_53 (nand_53_out, nand_34_out, nand_34_out);
  nand nand_54 (nand_54_out, 1'b1, c);
  nand nand_55 (nand_55_out, nand_35_out, nand_35_out);
  nand nand_56 (nand_56_out, nand_36_out, nand_36_out);
  nand nand_57 (nand_57_out, nand_37_out, nand_37_out);
  nand nand_58 (nand_58_out, 1'b1, c);
  nand nand_59 (nand_59_out, nand_38_out, nand_38_out);
  nand nand_60 (nand_60_out, 1'b1, c);
  nand nand_61 (o1, nand_39_out, nand_40_out);
  nand nand_62 (o2, nand_41_out, nand_42_out);
  nand nand_63 (nand_63_out, nand_43_out, c);
  nand nand_64 (nand_64_out, nand_44_out, c);
  nand nand_65 (nand_65_out, nand_45_out, nand_46_out);
  nand nand_66 (nand_66_out, nand_47_out, nand_48_out);
  nand nand_67 (nand_67_out, nand_49_out, c);
  nand nand_68 (nand_68_out, nand_50_out, c);
  nand nand_69 (nand_69_out, nand_51_out, nand_52_out);
  nand nand_70 (nand_70_out, nand_53_out, nand_54_out);
  nand nand_71 (nand_71_out, nand_55_out, c);
  nand nand_72 (nand_72_out, nand_56_out, c);
  nand nand_73 (nand_73_out, nand_57_out, nand_58_out);
  nand nand_74 (nand_74_out, nand_59_out, nand_60_out);
  nand nand_75 (o3, nand_63_out, nand_64_out);
  nand nand_76 (o4, nand_65_out, nand_66_out);
  nand nand_77 (o5, nand_67_out, nand_68_out);
  nand nand_78 (o6, nand_69_out, nand_70_out);
  nand nand_79 (o7, nand_71_out, nand_72_out);
  nand nand_80 (o8, nand_73_out, nand_74_out);
endmodule
