// Logisim project CPU_DEF.circ as structural Verilog: 29 circuits, main circuit CPU
module CPU (
  input  in_1,
  input  in_2,
  input  in_3,
  input  [7:0] in_4,
  output [7:0] out_5,
  output [7:0] out_6,
  output [7:0] out_7,
  output [7:0] out_8,
  output [7:0] out_9
);

  wire clock_1_out, control_unit_1_acc_e, control_unit_1_bus_1, control_unit_1_iar_s, control_unit_1_ir_s,
       control_unit_1_out_6, control_unit_1_out_8, control_unit_1_out_11, control_unit_1_out_12,
       control_unit_1_r0_e, control_unit_1_r0_s, control_unit_1_r1_e, control_unit_1_r1_s,
       control_unit_1_r2_e, control_unit_1_r2_s, control_unit_1_r3_e, control_unit_1_r3_s,
       control_unit_1_ram_e, control_unit_1_ram_s, cpu_clock_1_clk, cpu_clock_1_clke, cpu_clock_1_clks;
  wire [7:0] alu_1_out_8, cpu_accum_1_o, cpu_bus_1_1_o, cpu_ir_1_o, cpu_temp_1_o;

  CPU_TEMP cpu_temp_1 (.i(cpu_accum_1_o), .s(control_unit_1_out_12), .o(cpu_temp_1_o));
  CPU_BUS_1 cpu_bus_1_1 (.bus_1_a6cd2c94(control_unit_1_bus_1), .i(cpu_temp_1_o), .o(cpu_bus_1_1_o));
  ALU alu_1 (
    .in_3(1'b0), .in_2(cpu_bus_1_1_o), .in_1(cpu_accum_1_o), .in_4(in_1), .in_5(in_2), .in_6(in_3),
    .out_8(alu_1_out_8));  // open: carry_out, zero, larger, equal
  CPU_ACCUM cpu_accum_1 (
    .i(alu_1_out_8), .s(control_unit_1_out_8), .e(control_unit_1_acc_e), .ACC(out_9), .o(cpu_accum_1_o));
  Clock clock_1 (.out(clock_1_out));
  CPU_CLOCK cpu_clock_1 (.CLKIN(clock_1_out), .CLKS(cpu_clock_1_clks), .CLKE(cpu_clock_1_clke), .CLK(cpu_clock_1_clk));
  CPU_REG cpu_reg_1 (
    .i(cpu_accum_1_o), .s(control_unit_1_r0_s), .e(control_unit_1_r0_e), .\reg (out_5), .o(cpu_accum_1_o));
  CPU_REG cpu_reg_2 (.i(cpu_accum_1_o), .s(1'b1), .e(control_unit_1_out_11), .o(cpu_accum_1_o));  // open: reg
  CPU_REG cpu_reg_3 (
    .i(cpu_accum_1_o), .s(control_unit_1_r1_s), .e(control_unit_1_r1_e), .\reg (out_6), .o(cpu_accum_1_o));
  CPU_REG cpu_reg_4 (
    .i(cpu_accum_1_o), .s(control_unit_1_r2_s), .e(control_unit_1_r2_e), .\reg (out_7), .o(cpu_accum_1_o));
  CPU_IR cpu_ir_1 (.i(cpu_accum_1_o), .s(control_unit_1_ir_s), .o(cpu_ir_1_o));
  CPU_REG cpu_reg_5 (
    .i(cpu_accum_1_o), .s(control_unit_1_r3_s), .e(control_unit_1_r3_e), .\reg (out_8), .o(cpu_accum_1_o));
  CONTROL_UNIT control_unit_1 (
    .in_1(cpu_clock_1_clks), .in_2(cpu_clock_1_clk), .in_3(cpu_clock_1_clke), .in_4(cpu_ir_1_o),
    .out_6(control_unit_1_out_6), .out_8(control_unit_1_out_8), .RAM_S(control_unit_1_ram_s),
    .out_12(control_unit_1_out_12), .R0_S(control_unit_1_r0_s), .R1_S(control_unit_1_r1_s),
    .R2_S(control_unit_1_r2_s), .R3_S(control_unit_1_r3_s), .IR_S(control_unit_1_ir_s),
    .IAR_S(control_unit_1_iar_s), .RAM_E(control_unit_1_ram_e), .ACC_E(control_unit_1_acc_e),
    .out_11(control_unit_1_out_11), .R0_E(control_unit_1_r0_e), .R1_E(control_unit_1_r1_e),
    .R2_E(control_unit_1_r2_e), .R3_E(control_unit_1_r3_e), .BUS_1(control_unit_1_bus_1));
  MEM_RAM_256BYTES mem_ram_256bytes_1 (
    .in_6(in_4), .in_2(cpu_accum_1_o), .SA(control_unit_1_out_6), .in_1(control_unit_1_ram_s),
    .in_3(control_unit_1_ram_e), .out_7(cpu_accum_1_o));  // open: in_5, out_58, out_74, out_90, out_106, out_122, out_10, out_26, out_42, out_138, out_154, out_170, out_186, out_202, out_218, out_234, out_250, out_59, out_75, out_91, out_107, out_123, out_11, out_27, out_43, out_139, out_155, out_171, out_187, out_203, out_219, out_235, out_251, out_60, out_76, out_92, out_108, out_124, out_12, out_28, out_44, out_140, out_156, out_172, out_188, out_204, out_220, out_236, out_252, out_61, out_77, out_93, out_109, out_125, out_13, out_29, out_45, out_141, out_157, out_173, out_189, out_205, out_221, out_237, out_253, out_62, out_78, out_94, out_110, out_126, out_14, out_30, out_46, out_142, out_158, out_174, out_190, out_206, out_222, out_238, out_254, out_63, out_79, out_95, out_111, out_127, out_15, out_31, out_47, out_143, out_159, out_175, out_191, out_207, out_223, out_239, out_255, out_64, out_80, out_96, out_112, out_128, out_16, out_32, out_48, out_144, out_160, out_176, out_192, out_208, out_224, out_240, out_256, out_65, out_81, out_97, out_113, out_129, out_17, out_33, out_49, out_145, out_161, out_177, out_193, out_209, out_225, out_241, out_257, out_66, out_82, out_98, out_114, out_130, out_18, out_34, out_50, out_146, out_162, out_178, out_194, out_210, out_226, out_242, out_258, out_67, out_83, out_99, out_115, out_131, out_19, out_35, out_51, out_147, out_163, out_179, out_195, out_211, out_227, out_243, out_259, out_68, out_84, out_100, out_116, out_132, out_20, out_36, out_52, out_148, out_164, out_180, out_196, out_212, out_228, out_244, out_260, out_69, out_85, out_101, out_117, out_133, out_21, out_37, out_53, out_149, out_165, out_181, out_197, out_213, out_229, out_245, out_261, out_70, out_86, out_102, out_118, out_134, out_22, out_38, out_54, out_150, out_166, out_182, out_198, out_214, out_230, out_246, out_262, out_71, out_87, out_103, out_119, out_135, out_23, out_39, out_55, out_151, out_167, out_183, out_199, out_215, out_231, out_247, out_263, out_56, out_72, out_88, out_104, out_120, out_8, out_24, out_40, out_136, out_152, out_168, out_184, out_200, out_216, out_232, out_248, out_57, out_73, out_89, out_105, out_121, out_9, out_25, out_41, out_137, out_153, out_169, out_185, out_201, out_217, out_233, out_249
endmodule

module MEM_BYTE (
  input  RESET,
  input  H,
  input  V,
  input  S,
  input  E,
  input  [7:0] in_6,
  output [7:0] op,
  output [7:0] out_8
);

  wire and_1_out, and_2_out, and_3_out, nand_1_out, nand_2_out, nand_3_out, nand_4_out, nand_5_out,
       nand_6_out, nand_7_out, nand_8_out, nand_9_out, nand_10_out, nand_11_out, nand_12_out, nand_13_out,
       nand_14_out, nand_15_out, nand_16_out, nand_18_out, nand_20_out, nand_22_out, nand_24_out,
       nand_26_out, nand_28_out, nand_30_out, nand_32_out, or_1_out;
  wire [7:0] and_4_out;

  and and_1 (and_1_out, H, V);
  or or_1 (or_1_out, RESET, and_2_out);
  and and_2 (and_2_out, and_1_out, S);
  and and_3 (and_3_out, and_1_out, E);
  nand nand_1 (nand_1_out, in_6[0], or_1_out);
  nand nand_2 (nand_2_out, in_6[1], or_1_out);
  nand nand_3 (nand_3_out, in_6[2], or_1_out);
  nand nand_4 (nand_4_out, in_6[3], or_1_out);
  nand nand_5 (nand_5_out, in_6[4], or_1_out);
  nand nand_6 (nand_6_out, in_6[5], or_1_out);
  nand nand_7 (nand_7_out, in_6[6], or_1_out);
  nand nand_8 (nand_8_out, in_6[7], or_1_out);
  nand nand_9 (nand_9_out, nand_1_out, or_1_out);
  nand nand_10 (nand_10_out, nand_2_out, or_1_out);
  nand nand_11 (nand_11_out, nand_3_out, or_1_out);
  nand nand_12 (nand_12_out, nand_4_out, or_1_out);
  nand nand_13 (nand_13_out, nand_5_out, or_1_out);
  nand nand_14 (nand_14_out, nand_6_out, or_1_out);
  nand nand_15 (nand_15_out, nand_7_out, or_1_out);
  nand nand_16 (nand_16_out, nand_8_out, or_1_out);
  nand nand_17 (op[0], nand_1_out, nand_18_out);
  nand nand_18 (nand_18_out, op[0], nand_9_out);
  nand nand_19 (op[1], nand_2_out, nand_20_out);
  nand nand_20 (nand_20_out, op[1], nand_10_out);
  nand nand_21 (op[2], nand_3_out, nand_22_out);
  nand nand_22 (nand_22_out, op[2], nand_11_out);
  nand nand_23 (op[3], nand_4_out, nand_24_out);
  nand nand_24 (nand_24_out, op[3], nand_12_out);
  nand nand_25 (op[4], nand_5_out, nand_26_out);
  nand nand_26 (nand_26_out, op[4], nand_13_out);
  nand nand_27 (op[5], nand_6_out, nand_28_out);
  nand nand_28 (nand_28_out, op[5], nand_14_out);
  nand nand_29 (op[6], nand_7_out, nand_30_out);
  nand nand_30 (nand_30_out, op[6], nand_15_out);
  nand nand_31 (op[7], nand_8_out, nand_32_out);
  nand nand_32 (nand_32_out, op[7], nand_16_out);
  and and_4 (and_4_out[0], op[0], and_3_out);
  and and_5 (and_4_out[1], op[1], and_3_out);
  and and_6 (and_4_out[2], op[2], and_3_out);
  and and_7 (and_4_out[3], op[3], and_3_out);
  and and_8 (and_4_out[4], op[4], and_3_out);
  and and_9 (and_4_out[5], op[5], and_3_out);
  and and_10 (and_4_out[6], op[6], and_3_out);
  and and_11 (and_4_out[7], op[7], and_3_out);
  assign out_8 = and_3_out ? and_4_out : 8'bz;  // Controlled_Buffer controlled_buffer_1

  // Notes on the sheet:
  //   ENABLE MEM
  //   REG
endmodule

module CPU_DEC_4_16 (
  input  [3:0] in_1,
  output L,
  output out_3,
  output out_4,
  output out_5,
  output out_6,
  output out_7,
  output out_8,
  output out_9,
  output out_10,
  output out_11,
  output out_12,
  output out_13,
  output out_14,
  output out_15,
  output out_16,
  output M
);

  wire not_1_out, not_2_out, not_3_out, not_4_out;

  not not_1 (not_1_out, in_1[0]);
  not not_2 (not_2_out, in_1[1]);
  not not_3 (not_3_out, in_1[2]);
  not not_4 (not_4_out, in_1[3]);
  and and_1 (L, not_4_out, not_3_out, not_2_out, not_1_out);
  and and_2 (out_3, not_4_out, not_3_out, not_2_out, in_1[0]);
  and and_3 (out_4, not_4_out, not_3_out, in_1[1], not_1_out);
  and and_4 (out_5, not_4_out, not_3_out, in_1[1], in_1[0]);
  and and_5 (out_6, not_4_out, in_1[2], not_2_out, not_1_out);
  and and_6 (out_7, not_4_out, in_1[2], not_2_out, in_1[0]);
  and and_7 (out_8, not_4_out, in_1[2], in_1[1], not_1_out);
  and and_8 (out_9, not_4_out, in_1[2], in_1[1], in_1[0]);
  and and_9 (out_10, in_1[3], not_3_out, not_2_out, not_1_out);
  and and_10 (out_11, in_1[3], not_3_out, not_2_out, in_1[0]);
  and and_11 (out_12, in_1[3], not_3_out, in_1[1], not_1_out);
  and and_12 (out_13, in_1[3], not_3_out, in_1[1], in_1[0]);
  and and_13 (out_14, in_1[3], in_1[2], not_2_out, not_1_out);
  and and_14 (out_15, in_1[3], in_1[2], not_2_out, in_1[0]);
  and and_15 (out_16, in_1[3], in_1[2], in_1[1], not_1_out);
  and and_16 (M, in_1[3], in_1[2], in_1[1], in_1[0]);

  // Notes on the sheet:
  //   out_13: pull=down
  //   out_14: pull=down
  //   out_15: pull=down
  //   out_16: pull=down
  //   M: pull=down
  //   L: pull=down
  //   out_3: pull=down
  //   out_4: pull=down
  //   out_5: pull=down
  //   out_6: pull=down
  //   out_7: pull=down
  //   out_8: pull=down
  //   out_9: pull=down
  //   out_10: pull=down
  //   out_11: pull=down
  //   out_12: pull=down
  //   in_1: pull=down
endmodule

module MEM_RAM_256BYTES (
  input  in_1,
  input  [7:0] in_2,
  input  in_3,
  input  SA,
  input  in_5,
  input  [7:0] in_6,
  output [7:0] out_7,
  output [7:0] out_8,
  output [7:0] out_9,
  output [7:0] out_10,
  output [7:0] out_11,
  output [7:0] out_12,
  output [7:0] out_13,
  output [7:0] out_14,
  output [7:0] out_15,
  output [7:0] out_16,
  output [7:0] out_17,
  output [7:0] out_18,
  output [7:0] out_19,
  output [7:0] out_20,
  output [7:0] out_21,
  output [7:0] out_22,
  output [7:0] out_23,
  output [7:0] out_24,
  output [7:0] out_25,
  output [7:0] out_26,
  output [7:0] out_27,
  output [7:0] out_28,
  output [7:0] out_29,
  output [7:0] out_30,
  output [7:0] out_31,
  output [7:0] out_32,
  output [7:0] out_33,
  output [7:0] out_34,
  output [7:0] out_35,
  output [7:0] out_36,
  output [7:0] out_37,
  output [7:0] out_38,
  output [7:0] out_39,
  output [7:0] out_40,
  output [7:0] out_41,
  output [7:0] out_42,
  output [7:0] out_43,
  output [7:0] out_44,
  output [7:0] out_45,
  output [7:0] out_46,
  output [7:0] out_47,
  output [7:0] out_48,
  output [7:0] out_49,
  output [7:0] out_50,
  output [7:0] out_51,
  output [7:0] out_52,
  output [7:0] out_53,
  output [7:0] out_54,
  output [7:0] out_55,
  output [7:0] out_56,
  output [7:0] out_57,
  output [7:0] out_58,
  output [7:0] out_59,
  output [7:0] out_60,
  output [7:0] out_61,
  output [7:0] out_62,
  output [7:0] out_63,
  output [7:0] out_64,
  output [7:0] out_65,
  output [7:0] out_66,
  output [7:0] out_67,
  output [7:0] out_68,
  output [7:0] out_69,
  output [7:0] out_70,
  output [7:0] out_71,
  output [7:0] out_72,
  output [7:0] out_73,
  output [7:0] out_74,
  output [7:0] out_75,
  output [7:0] out_76,
  output [7:0] out_77,
  output [7:0] out_78,
  output [7:0] out_79,
  output [7:0] out_80,
  output [7:0] out_81,
  output [7:0] out_82,
  output [7:0] out_83,
  output [7:0] out_84,
  output [7:0] out_85,
  output [7:0] out_86,
  output [7:0] out_87,
  output [7:0] out_88,
  output [7:0] out_89,
  output [7:0] out_90,
  output [7:0] out_91,
  output [7:0] out_92,
  output [7:0] out_93,
  output [7:0] out_94,
  output [7:0] out_95,
  output [7:0] out_96,
  output [7:0] out_97,
  output [7:0] out_98,
  output [7:0] out_99,
  output [7:0] out_100,
  output [7:0] out_101,
  output [7:0] out_102,
  output [7:0] out_103,
  output [7:0] out_104,
  output [7:0] out_105,
  output [7:0] out_106,
  output [7:0] out_107,
  output [7:0] out_108,
  output [7:0] out_109,
  output [7:0] out_110,
  output [7:0] out_111,
  output [7:0] out_112,
  output [7:0] out_113,
  output [7:0] out_114,
  output [7:0] out_115,
  output [7:0] out_116,
  output [7:0] out_117,
  output [7:0] out_118,
  output [7:0] out_119,
  output [7:0] out_120,
  output [7:0] out_121,
  output [7:0] out_122,
  output [7:0] out_123,
  output [7:0] out_124,
  output [7:0] out_125,
  output [7:0] out_126,
  output [7:0] out_127,
  output [7:0] out_128,
  output [7:0] out_129,
  output [7:0] out_130,
  output [7:0] out_131,
  output [7:0] out_132,
  output [7:0] out_133,
  output [7:0] out_134,
  output [7:0] out_135,
  output [7:0] out_136,
  output [7:0] out_137,
  output [7:0] out_138,
  output [7:0] out_139,
  output [7:0] out_140,
  output [7:0] out_141,
  output [7:0] out_142,
  output [7:0] out_143,
  output [7:0] out_144,
  output [7:0] out_145,
  output [7:0] out_146,
  output [7:0] out_147,
  output [7:0] out_148,
  output [7:0] out_149,
  output [7:0] out_150,
  output [7:0] out_151,
  output [7:0] out_152,
  output [7:0] out_153,
  output [7:0] out_154,
  output [7:0] out_155,
  output [7:0] out_156,
  output [7:0] out_157,
  output [7:0] out_158,
  output [7:0] out_159,
  output [7:0] out_160,
  output [7:0] out_161,
  output [7:0] out_162,
  output [7:0] out_163,
  output [7:0] out_164,
  output [7:0] out_165,
  output [7:0] out_166,
  output [7:0] out_167,
  output [7:0] out_168,
  output [7:0] out_169,
  output [7:0] out_170,
  output [7:0] out_171,
  output [7:0] out_172,
  output [7:0] out_173,
  output [7:0] out_174,
  output [7:0] out_175,
  output [7:0] out_176,
  output [7:0] out_177,
  output [7:0] out_178,
  output [7:0] out_179,
  output [7:0] out_180,
  output [7:0] out_181,
  output [7:0] out_182,
  output [7:0] out_183,
  output [7:0] out_184,
  output [7:0] out_185,
  output [7:0] out_186,
  output [7:0] out_187,
  output [7:0] out_188,
  output [7:0] out_189,
  output [7:0] out_190,
  output [7:0] out_191,
  output [7:0] out_192,
  output [7:0] out_193,
  output [7:0] out_194,
  output [7:0] out_195,
  output [7:0] out_196,
  output [7:0] out_197,
  output [7:0] out_198,
  output [7:0] out_199,
  output [7:0] out_200,
  output [7:0] out_201,
  output [7:0] out_202,
  output [7:0] out_203,
  output [7:0] out_204,
  output [7:0] out_205,
  output [7:0] out_206,
  output [7:0] out_207,
  output [7:0] out_208,
  output [7:0] out_209,
  output [7:0] out_210,
  output [7:0] out_211,
  output [7:0] out_212,
  output [7:0] out_213,
  output [7:0] out_214,
  output [7:0] out_215,
  output [7:0] out_216,
  output [7:0] out_217,
  output [7:0] out_218,
  output [7:0] out_219,
  output [7:0] out_220,
  output [7:0] out_221,
  output [7:0] out_222,
  output [7:0] out_223,
  output [7:0] out_224,
  output [7:0] out_225,
  output [7:0] out_226,
  output [7:0] out_227,
  output [7:0] out_228,
  output [7:0] out_229,
  output [7:0] out_230,
  output [7:0] out_231,
  output [7:0] out_232,
  output [7:0] out_233,
  output [7:0] out_234,
  output [7:0] out_235,
  output [7:0] out_236,
  output [7:0] out_237,
  output [7:0] out_238,
  output [7:0] out_239,
  output [7:0] out_240,
  output [7:0] out_241,
  output [7:0] out_242,
  output [7:0] out_243,
  output [7:0] out_244,
  output [7:0] out_245,
  output [7:0] out_246,
  output [7:0] out_247,
  output [7:0] out_248,
  output [7:0] out_249,
  output [7:0] out_250,
  output [7:0] out_251,
  output [7:0] out_252,
  output [7:0] out_253,
  output [7:0] out_254,
  output [7:0] out_255,
  output [7:0] out_256,
  output [7:0] out_257,
  output [7:0] out_258,
  output [7:0] out_259,
  output [7:0] out_260,
  output [7:0] out_261,
  output [7:0] out_262,
  output [7:0] out_263
);

  wire H0, H1, H2, H3, H4, H5, H6, H7, H8, H9, H10, H11, H12, H13, H14, H15, V0, V1, V2, V3, V4, V5, V6, V7,
       V8, V9, V10, V11, V12, V13, V14, V15;
  wire [7:0] mem_8_bits_1_out_3;

  MEM_8_BITS mem_8_bits_1 (.in_1(in_2), .s(SA), .out_3(mem_8_bits_1_out_3));
  CPU_DEC_4_16 cpu_dec_4_16_1 (
    .in_1(mem_8_bits_1_out_3[7:4]), .out_13(H11), .out_14(H12), .out_15(H13), .out_16(H14), .M(H15), .L(H0),
    .out_3(H1), .out_4(H2), .out_5(H3), .out_6(H4), .out_7(H5), .out_8(H6), .out_9(H7), .out_10(H8),
    .out_11(H9), .out_12(H10));
  MEM_BYTE mem_byte_1 (.H(H0), .V(V15), .S(in_1), .E(in_3), .RESET(in_5), .in_6(in_6), .out_8(out_7), .op(out_8));
  MEM_BYTE mem_byte_2 (.H(H1), .V(V15), .S(in_1), .E(in_3), .RESET(in_5), .in_6(in_6), .out_8(out_7), .op(out_24));
  MEM_BYTE mem_byte_3 (.H(H2), .V(V15), .S(in_1), .E(in_3), .RESET(in_5), .in_6(in_6), .out_8(out_7), .op(out_40));
  MEM_BYTE mem_byte_4 (.H(H3), .V(V15), .S(in_1), .E(in_3), .RESET(in_5), .in_6(in_6), .out_8(out_7), .op(out_56));
  MEM_BYTE mem_byte_5 (.H(H4), .V(V15), .S(in_1), .E(in_3), .RESET(in_5), .in_6(in_6), .out_8(out_7), .op(out_72));
  MEM_BYTE mem_byte_6 (.H(H5), .V(V15), .S(in_1), .E(in_3), .RESET(in_5), .in_6(in_6), .out_8(out_7), .op(out_88));
  MEM_BYTE mem_byte_7 (.H(H6), .V(V15), .S(in_1), .E(in_3), .RESET(in_5), .in_6(in_6), .out_8(out_7), .op(out_104));
  MEM_BYTE mem_byte_8 (.H(H7), .V(V15), .S(in_1), .E(in_3), .RESET(in_5), .in_6(in_6), .out_8(out_7), .op(out_120));
  MEM_BYTE mem_byte_9 (.H(H8), .V(V15), .S(in_1), .E(in_3), .RESET(in_5), .in_6(in_6), .out_8(out_7), .op(out_136));
  MEM_BYTE mem_byte_10 (.H(H9), .V(V15), .S(in_1), .E(in_3), .RESET(in_5), .in_6(in_6), .out_8(out_7), .op(out_152));
  MEM_BYTE mem_byte_11 (.H(H10), .V(V15), .S(in_1), .E(in_3), .RESET(in_5), .in_6(in_6), .out_8(out_7), .op(out_168));
  MEM_BYTE mem_byte_12 (.H(H11), .V(V15), .S(in_1), .E(in_3), .RESET(in_5), .in_6(in_6), .out_8(out_7), .op(out_184));
  MEM_BYTE mem_byte_13 (.H(H12), .V(V15), .S(in_1), .E(in_3), .RESET(in_5), .in_6(in_6), .out_8(out_7), .op(out_200));
  MEM_BYTE mem_byte_14 (.H(H13), .V(V15), .S(in_1), .E(in_3), .RESET(in_5), .in_6(in_6), .out_8(out_7), .op(out_216));
  MEM_BYTE mem_byte_15 (.H(H14), .V(V15), .S(in_1), .E(in_3), .RESET(in_5), .in_6(in_6), .out_8(out_7), .op(out_232));
  MEM_BYTE mem_byte_16 (.H(H15), .V(V15), .S(in_1), .E(in_3), .RESET(in_5), .in_6(in_6), .out_8(out_7), .op(out_248));
  MEM_BYTE mem_byte_17 (.H(H0), .V(V14), .S(in_1), .E(in_3), .RESET(in_5), .in_6(in_6), .out_8(out_7), .op(out_9));
  MEM_BYTE mem_byte_18 (.H(H1), .V(V14), .S(in_1), .E(in_3), .RESET(in_5), .in_6(in_6), .out_8(out_7), .op(out_25));
  MEM_BYTE mem_byte_19 (.H(H2), .V(V14), .S(in_1), .E(in_3), .RESET(in_5), .in_6(in_6), .out_8(out_7), .op(out_41));
  MEM_BYTE mem_byte_20 (.H(H3), .V(V14), .S(in_1), .E(in_3), .RESET(in_5), .in_6(in_6), .out_8(out_7), .op(out_57));
  MEM_BYTE mem_byte_21 (.H(H4), .V(V14), .S(in_1), .E(in_3), .RESET(in_5), .in_6(in_6), .out_8(out_7), .op(out_73));
  MEM_BYTE mem_byte_22 (.H(H5), .V(V14), .S(in_1), .E(in_3), .RESET(in_5), .in_6(in_6), .out_8(out_7), .op(out_89));
  MEM_BYTE mem_byte_23 (.H(H6), .V(V14), .S(in_1), .E(in_3), .RESET(in_5), .in_6(in_6), .out_8(out_7), .op(out_105));
  MEM_BYTE mem_byte_24 (.H(H7), .V(V14), .S(in_1), .E(in_3), .RESET(in_5), .in_6(in_6), .out_8(out_7), .op(out_121));
  MEM_BYTE mem_byte_25 (.H(H8), .V(V14), .S(in_1), .E(in_3), .RESET(in_5), .in_6(in_6), .out_8(out_7), .op(out_137));
  MEM_BYTE mem_byte_26 (.H(H9), .V(V14), .S(in_1), .E(in_3), .RESET(in_5), .in_6(in_6), .out_8(out_7), .op(out_153));
  MEM_BYTE mem_byte_27 (.H(H10), .V(V14), .S(in_1), .E(in_3), .RESET(in_5), .in_6(in_6), .out_8(out_7), .op(out_169));
  MEM_BYTE mem_byte_28 (.H(H11), .V(V14), .S(in_1), .E(in_3), .RESET(in_5), .in_6(in_6), .out_8(out_7), .op(out_185));
  MEM_BYTE mem_byte_29 (.H(H12), .V(V14), .S(in_1), .E(in_3), .RESET(in_5), .in_6(in_6), .out_8(out_7), .op(out_201));
  MEM_BYTE mem_byte_30 (.H(H13), .V(V14), .S(in_1), .E(in_3), .RESET(in_5), .in_6(in_6), .out_8(out_7), .op(out_217));
  MEM_BYTE mem_byte_31 (.H(H14), .V(V14), .S(in_1), .E(in_3), .RESET(in_5), .in_6(in_6), .out_8(out_7), .op(out_233));
  MEM_BYTE mem_byte_32 (.H(H15), .V(V14), .S(in_1), .E(in_3), .RESET(in_5), .in_6(in_6), .out_8(out_7), .op(out_249));
  MEM_BYTE mem_byte_33 (.H(H0), .V(V13), .S(in_1), .E(in_3), .RESET(in_5), .in_6(in_6), .out_8(out_7), .op(out_10));
  MEM_BYTE mem_byte_34 (.H(H1), .V(V13), .S(in_1), .E(in_3), .RESET(in_5), .in_6(in_6), .out_8(out_7), .op(out_26));
  MEM_BYTE mem_byte_35 (.H(H2), .V(V13), .S(in_1), .E(in_3), .RESET(in_5), .in_6(in_6), .out_8(out_7), .op(out_42));
  MEM_BYTE mem_byte_36 (.H(H3), .V(V13), .S(in_1), .E(in_3), .RESET(in_5), .in_6(in_6), .out_8(out_7), .op(out_58));
  MEM_BYTE mem_byte_37 (.H(H4), .V(V13), .S(in_1), .E(in_3), .RESET(in_5), .in_6(in_6), .out_8(out_7), .op(out_74));
  MEM_BYTE mem_byte_38 (.H(H5), .V(V13), .S(in_1), .E(in_3), .RESET(in_5), .in_6(in_6), .out_8(out_7), .op(out_90));
  MEM_BYTE mem_byte_39 (.H(H6), .V(V13), .S(in_1), .E(in_3), .RESET(in_5), .in_6(in_6), .out_8(out_7), .op(out_106));
  MEM_BYTE mem_byte_40 (.H(H7), .V(V13), .S(in_1), .E(in_3), .RESET(in_5), .in_6(in_6), .out_8(out_7), .op(out_122));
  MEM_BYTE mem_byte_41 (.H(H8), .V(V13), .S(in_1), .E(in_3), .RESET(in_5), .in_6(in_6), .out_8(out_7), .op(out_138));
  MEM_BYTE mem_byte_42 (.H(H9), .V(V13), .S(in_1), .E(in_3), .RESET(in_5), .in_6(in_6), .out_8(out_7), .op(out_154));
  MEM_BYTE mem_byte_43 (.H(H10), .V(V13), .S(in_1), .E(in_3), .RESET(in_5), .in_6(in_6), .out_8(out_7), .op(out_170));
  MEM_BYTE mem_byte_44 (.H(H11), .V(V13), .S(in_1), .E(in_3), .RESET(in_5), .in_6(in_6), .out_8(out_7), .op(out_186));
  MEM_BYTE mem_byte_45 (.H(H12), .V(V13), .S(in_1), .E(in_3), .RESET(in_5), .in_6(in_6), .out_8(out_7), .op(out_202));
  MEM_BYTE mem_byte_46 (.H(H13), .V(V13), .S(in_1), .E(in_3), .RESET(in_5), .in_6(in_6), .out_8(out_7), .op(out_218));
  MEM_BYTE mem_byte_47 (.H(H14), .V(V13), .S(in_1), .E(in_3), .RESET(in_5), .in_6(in_6), .out_8(out_7), .op(out_234));
  MEM_BYTE mem_byte_48 (.H(H15), .V(V13), .S(in_1), .E(in_3), .RESET(in_5), .in_6(in_6), .out_8(out_7), .op(out_250));
  MEM_BYTE mem_byte_49 (.H(H0), .V(V12), .S(in_1), .E(in_3), .RESET(in_5), .in_6(in_6), .out_8(out_7), .op(out_11));
  MEM_BYTE mem_byte_50 (.H(H1), .V(V12), .S(in_1), .E(in_3), .RESET(in_5), .in_6(in_6), .out_8(out_7), .op(out_27));
  MEM_BYTE mem_byte_51 (.H(H2), .V(V12), .S(in_1), .E(in_3), .RESET(in_5), .in_6(in_6), .out_8(out_7), .op(out_43));
  MEM_BYTE mem_byte_52 (.H(H3), .V(V12), .S(in_1), .E(in_3), .RESET(in_5), .in_6(in_6), .out_8(out_7), .op(out_59));
  MEM_BYTE mem_byte_53 (.H(H4), .V(V12), .S(in_1), .E(in_3), .RESET(in_5), .in_6(in_6), .out_8(out_7), .op(out_75));
  MEM_BYTE mem_byte_54 (.H(H5), .V(V12), .S(in_1), .E(in_3), .RESET(in_5), .in_6(in_6), .out_8(out_7), .op(out_91));
  MEM_BYTE mem_byte_55 (.H(H6), .V(V12), .S(in_1), .E(in_3), .RESET(in_5), .in_6(in_6), .out_8(out_7), .op(out_107));
  MEM_BYTE mem_byte_56 (.H(H7), .V(V12), .S(in_1), .E(in_3), .RESET(in_5), .in_6(in_6), .out_8(out_7), .op(out_123));
  MEM_BYTE mem_byte_57 (.H(H8), .V(V12), .S(in_1), .E(in_3), .RESET(in_5), .in_6(in_6), .out_8(out_7), .op(out_139));
  MEM_BYTE mem_byte_58 (.H(H9), .V(V12), .S(in_1), .E(in_3), .RESET(in_5), .in_6(in_6), .out_8(out_7), .op(out_155));
  MEM_BYTE mem_byte_59 (.H(H10), .V(V12), .S(in_1), .E(in_3), .RESET(in_5), .in_6(in_6), .out_8(out_7), .op(out_171));
  MEM_BYTE mem_byte_60 (.H(H11), .V(V12), .S(in_1), .E(in_3), .RESET(in_5), .in_6(in_6), .out_8(out_7), .op(out_187));
  MEM_BYTE mem_byte_61 (.H(H12), .V(V12), .S(in_1), .E(in_3), .RESET(in_5), .in_6(in_6), .out_8(out_7), .op(out_203));
  MEM_BYTE mem_byte_62 (.H(H13), .V(V12), .S(in_1), .E(in_3), .RESET(in_5), .in_6(in_6), .out_8(out_7), .op(out_219));
  MEM_BYTE mem_byte_63 (.H(H14), .V(V12), .S(in_1), .E(in_3), .RESET(in_5), .in_6(in_6), .out_8(out_7), .op(out_235));
  MEM_BYTE mem_byte_64 (.H(H15), .V(V12), .S(in_1), .E(in_3), .RESET(in_5), .in_6(in_6), .out_8(out_7), .op(out_251));
  MEM_BYTE mem_byte_65 (.H(H0), .V(V11), .S(in_1), .E(in_3), .RESET(in_5), .in_6(in_6), .out_8(out_7), .op(out_12));
  MEM_BYTE mem_byte_66 (.H(H1), .V(V11), .S(in_1), .E(in_3), .RESET(in_5), .in_6(in_6), .out_8(out_7), .op(out_28));
  MEM_BYTE mem_byte_67 (.H(H2), .V(V11), .S(in_1), .E(in_3), .RESET(in_5), .in_6(in_6), .out_8(out_7), .op(out_44));
  MEM_BYTE mem_byte_68 (.H(H3), .V(V11), .S(in_1), .E(in_3), .RESET(in_5), .in_6(in_6), .out_8(out_7), .op(out_60));
  MEM_BYTE mem_byte_69 (.H(H4), .V(V11), .S(in_1), .E(in_3), .RESET(in_5), .in_6(in_6), .out_8(out_7), .op(out_76));
  MEM_BYTE mem_byte_70 (.H(H5), .V(V11), .S(in_1), .E(in_3), .RESET(in_5), .in_6(in_6), .out_8(out_7), .op(out_92));
  MEM_BYTE mem_byte_71 (.H(H6), .V(V11), .S(in_1), .E(in_3), .RESET(in_5), .in_6(in_6), .out_8(out_7), .op(out_108));
  MEM_BYTE mem_byte_72 (.H(H7), .V(V11), .S(in_1), .E(in_3), .RESET(in_5), .in_6(in_6), .out_8(out_7), .op(out_124));
  MEM_BYTE mem_byte_73 (.H(H8), .V(V11), .S(in_1), .E(in_3), .RESET(in_5), .in_6(in_6), .out_8(out_7), .op(out_140));
  MEM_BYTE mem_byte_74 (.H(H9), .V(V11), .S(in_1), .E(in_3), .RESET(in_5), .in_6(in_6), .out_8(out_7), .op(out_156));
  MEM_BYTE mem_byte_75 (.H(H10), .V(V11), .S(in_1), .E(in_3), .RESET(in_5), .in_6(in_6), .out_8(out_7), .op(out_172));
  MEM_BYTE mem_byte_76 (.H(H11), .V(V11), .S(in_1), .E(in_3), .RESET(in_5), .in_6(in_6), .out_8(out_7), .op(out_188));
  MEM_BYTE mem_byte_77 (.H(H12), .V(V11), .S(in_1), .E(in_3), .RESET(in_5), .in_6(in_6), .out_8(out_7), .op(out_204));
  MEM_BYTE mem_byte_78 (.H(H13), .V(V11), .S(in_1), .E(in_3), .RESET(in_5), .in_6(in_6), .out_8(out_7), .op(out_220));
  MEM_BYTE mem_byte_79 (.H(H14), .V(V11), .S(in_1), .E(in_3), .RESET(in_5), .in_6(in_6), .out_8(out_7), .op(out_236));
  MEM_BYTE mem_byte_80 (.H(H15), .V(V11), .S(in_1), .E(in_3), .RESET(in_5), .in_6(in_6), .out_8(out_7), .op(out_252));
  MEM_BYTE mem_byte_81 (.H(H0), .V(V10), .S(in_1), .E(in_3), .RESET(in_5), .in_6(in_6), .out_8(out_7), .op(out_13));
  MEM_BYTE mem_byte_82 (.H(H1), .V(V10), .S(in_1), .E(in_3), .RESET(in_5), .in_6(in_6), .out_8(out_7), .op(out_29));
  MEM_BYTE mem_byte_83 (.H(H2), .V(V10), .S(in_1), .E(in_3), .RESET(in_5), .in_6(in_6), .out_8(out_7), .op(out_45));
  MEM_BYTE mem_byte_84 (.H(H3), .V(V10), .S(in_1), .E(in_3), .RESET(in_5), .in_6(in_6), .out_8(out_7), .op(out_61));
  MEM_BYTE mem_byte_85 (.H(H4), .V(V10), .S(in_1), .E(in_3), .RESET(in_5), .in_6(in_6), .out_8(out_7), .op(out_77));
  MEM_BYTE mem_byte_86 (.H(H5), .V(V10), .S(in_1), .E(in_3), .RESET(in_5), .in_6(in_6), .out_8(out_7), .op(out_93));
  MEM_BYTE mem_byte_87 (.H(H6), .V(V10), .S(in_1), .E(in_3), .RESET(in_5), .in_6(in_6), .out_8(out_7), .op(out_109));
  MEM_BYTE mem_byte_88 (.H(H7), .V(V10), .S(in_1), .E(in_3), .RESET(in_5), .in_6(in_6), .out_8(out_7), .op(out_125));
  MEM_BYTE mem_byte_89 (.H(H8), .V(V10), .S(in_1), .E(in_3), .RESET(in_5), .in_6(in_6), .out_8(out_7), .op(out_141));
  MEM_BYTE mem_byte_90 (.H(H9), .V(V10), .S(in_1), .E(in_3), .RESET(in_5), .in_6(in_6), .out_8(out_7), .op(out_157));
  MEM_BYTE mem_byte_91 (.H(H10), .V(V10), .S(in_1), .E(in_3), .RESET(in_5), .in_6(in_6), .out_8(out_7), .op(out_173));
  MEM_BYTE mem_byte_92 (.H(H11), .V(V10), .S(in_1), .E(in_3), .RESET(in_5), .in_6(in_6), .out_8(out_7), .op(out_189));
  MEM_BYTE mem_byte_93 (.H(H12), .V(V10), .S(in_1), .E(in_3), .RESET(in_5), .in_6(in_6), .out_8(out_7), .op(out_205));
  MEM_BYTE mem_byte_94 (.H(H13), .V(V10), .S(in_1), .E(in_3), .RESET(in_5), .in_6(in_6), .out_8(out_7), .op(out_221));
  MEM_BYTE mem_byte_95 (.H(H14), .V(V10), .S(in_1), .E(in_3), .RESET(in_5), .in_6(in_6), .out_8(out_7), .op(out_237));
  MEM_BYTE mem_byte_96 (.H(H15), .V(V0), .S(in_1), .E(in_3), .RESET(in_5), .in_6(in_6), .out_8(out_7), .op(out_253));
  MEM_BYTE mem_byte_97 (.H(H0), .V(V9), .S(in_1), .E(in_3), .RESET(in_5), .in_6(in_6), .out_8(out_7), .op(out_14));
  MEM_BYTE mem_byte_98 (.H(H1), .V(V9), .S(in_1), .E(in_3), .RESET(in_5), .in_6(in_6), .out_8(out_7), .op(out_30));
  MEM_BYTE mem_byte_99 (.H(H2), .V(V9), .S(in_1), .E(in_3), .RESET(in_5), .in_6(in_6), .out_8(out_7), .op(out_46));
  MEM_BYTE mem_byte_100 (.H(H3), .V(V9), .S(in_1), .E(in_3), .RESET(in_5), .in_6(in_6), .out_8(out_7), .op(out_62));
  MEM_BYTE mem_byte_101 (.H(H4), .V(V9), .S(in_1), .E(in_3), .RESET(in_5), .in_6(in_6), .out_8(out_7), .op(out_78));
  MEM_BYTE mem_byte_102 (.H(H5), .V(V9), .S(in_1), .E(in_3), .RESET(in_5), .in_6(in_6), .out_8(out_7), .op(out_94));
  MEM_BYTE mem_byte_103 (.H(H6), .V(V9), .S(in_1), .E(in_3), .RESET(in_5), .in_6(in_6), .out_8(out_7), .op(out_110));
  MEM_BYTE mem_byte_104 (.H(H7), .V(V9), .S(in_1), .E(in_3), .RESET(in_5), .in_6(in_6), .out_8(out_7), .op(out_126));
  MEM_BYTE mem_byte_105 (.H(H8), .V(V9), .S(in_1), .E(in_3), .RESET(in_5), .in_6(in_6), .out_8(out_7), .op(out_142));
  MEM_BYTE mem_byte_106 (.H(H9), .V(V9), .S(in_1), .E(in_3), .RESET(in_5), .in_6(in_6), .out_8(out_7), .op(out_158));
  MEM_BYTE mem_byte_107 (.H(H10), .V(V9), .S(in_1), .E(in_3), .RESET(in_5), .in_6(in_6), .out_8(out_7), .op(out_174));
  MEM_BYTE mem_byte_108 (.H(H11), .V(V9), .S(in_1), .E(in_3), .RESET(in_5), .in_6(in_6), .out_8(out_7), .op(out_190));
  MEM_BYTE mem_byte_109 (.H(H12), .V(V9), .S(in_1), .E(in_3), .RESET(in_5), .in_6(in_6), .out_8(out_7), .op(out_206));
  MEM_BYTE mem_byte_110 (.H(H13), .V(V9), .S(in_1), .E(in_3), .RESET(in_5), .in_6(in_6), .out_8(out_7), .op(out_222));
  MEM_BYTE mem_byte_111 (.H(H14), .V(V9), .S(in_1), .E(in_3), .RESET(in_5), .in_6(in_6), .out_8(out_7), .op(out_238));
  MEM_BYTE mem_byte_112 (.H(H15), .V(V9), .S(in_1), .E(in_3), .RESET(in_5), .in_6(in_6), .out_8(out_7), .op(out_254));
  MEM_BYTE mem_byte_113 (.H(H0), .V(V8), .S(in_1), .E(in_3), .RESET(in_5), .in_6(in_6), .out_8(out_7), .op(out_15));
  MEM_BYTE mem_byte_114 (.H(H1), .V(V8), .S(in_1), .E(in_3), .RESET(in_5), .in_6(in_6), .out_8(out_7), .op(out_31));
  MEM_BYTE mem_byte_115 (.H(H2), .V(V8), .S(in_1), .E(in_3), .RESET(in_5), .in_6(in_6), .out_8(out_7), .op(out_47));
  MEM_BYTE mem_byte_116 (.H(H3), .V(V8), .S(in_1), .E(in_3), .RESET(in_5), .in_6(in_6), .out_8(out_7), .op(out_63));
  MEM_BYTE mem_byte_117 (.H(H4), .V(V8), .S(in_1), .E(in_3), .RESET(in_5), .in_6(in_6), .out_8(out_7), .op(out_79));
  MEM_BYTE mem_byte_118 (.H(H5), .V(V8), .S(in_1), .E(in_3), .RESET(in_5), .in_6(in_6), .out_8(out_7), .op(out_95));
  MEM_BYTE mem_byte_119 (.H(H6), .V(V8), .S(in_1), .E(in_3), .RESET(in_5), .in_6(in_6), .out_8(out_7), .op(out_111));
  MEM_BYTE mem_byte_120 (.H(H7), .V(V8), .S(in_1), .E(in_3), .RESET(in_5), .in_6(in_6), .out_8(out_7), .op(out_127));
  MEM_BYTE mem_byte_121 (.H(H8), .V(V8), .S(in_1), .E(in_3), .RESET(in_5), .in_6(in_6), .out_8(out_7), .op(out_143));
  MEM_BYTE mem_byte_122 (.H(H9), .V(V8), .S(in_1), .E(in_3), .RESET(in_5), .in_6(in_6), .out_8(out_7), .op(out_159));
  MEM_BYTE mem_byte_123 (.H(H10), .V(V8), .S(in_1), .E(in_3), .RESET(in_5), .in_6(in_6), .out_8(out_7), .op(out_175));
  MEM_BYTE mem_byte_124 (.H(H11), .V(V8), .S(in_1), .E(in_3), .RESET(in_5), .in_6(in_6), .out_8(out_7), .op(out_191));
  MEM_BYTE mem_byte_125 (.H(H12), .V(V8), .S(in_1), .E(in_3), .RESET(in_5), .in_6(in_6), .out_8(out_7), .op(out_207));
  MEM_BYTE mem_byte_126 (.H(H13), .V(V8), .S(in_1), .E(in_3), .RESET(in_5), .in_6(in_6), .out_8(out_7), .op(out_223));
  MEM_BYTE mem_byte_127 (.H(H14), .V(V8), .S(in_1), .E(in_3), .RESET(in_5), .in_6(in_6), .out_8(out_7), .op(out_239));
  MEM_BYTE mem_byte_128 (.H(H15), .V(V8), .S(in_1), .E(in_3), .RESET(in_5), .in_6(in_6), .out_8(out_7), .op(out_255));
  MEM_BYTE mem_byte_129 (.H(H0), .V(V7), .S(in_1), .E(in_3), .RESET(in_5), .in_6(in_6), .out_8(out_7), .op(out_16));
  MEM_BYTE mem_byte_130 (.H(H1), .V(V7), .S(in_1), .E(in_3), .RESET(in_5), .in_6(in_6), .out_8(out_7), .op(out_32));
  MEM_BYTE mem_byte_131 (.H(H2), .V(V7), .S(in_1), .E(in_3), .RESET(in_5), .in_6(in_6), .out_8(out_7), .op(out_48));
  MEM_BYTE mem_byte_132 (.H(H3), .V(V7), .S(in_1), .E(in_3), .RESET(in_5), .in_6(in_6), .out_8(out_7), .op(out_64));
  MEM_BYTE mem_byte_133 (.H(H4), .V(V7), .S(in_1), .E(in_3), .RESET(in_5), .in_6(in_6), .out_8(out_7), .op(out_80));
  MEM_BYTE mem_byte_134 (.H(H5), .V(V7), .S(in_1), .E(in_3), .RESET(in_5), .in_6(in_6), .out_8(out_7), .op(out_96));
  MEM_BYTE mem_byte_135 (.H(H6), .V(V7), .S(in_1), .E(in_3), .RESET(in_5), .in_6(in_6), .out_8(out_7), .op(out_112));
  MEM_BYTE mem_byte_136 (.H(H7), .V(V7), .S(in_1), .E(in_3), .RESET(in_5), .in_6(in_6), .out_8(out_7), .op(out_128));
  MEM_BYTE mem_byte_137 (.H(H8), .V(V7), .S(in_1), .E(in_3), .RESET(in_5), .in_6(in_6), .out_8(out_7), .op(out_144));
  MEM_BYTE mem_byte_138 (.H(H9), .V(V7), .S(in_1), .E(in_3), .RESET(in_5), .in_6(in_6), .out_8(out_7), .op(out_160));
  MEM_BYTE mem_byte_139 (.H(H10), .V(V7), .S(in_1), .E(in_3), .RESET(in_5), .in_6(in_6), .out_8(out_7), .op(out_176));
  MEM_BYTE mem_byte_140 (.H(H11), .V(V7), .S(in_1), .E(in_3), .RESET(in_5), .in_6(in_6), .out_8(out_7), .op(out_192));
  MEM_BYTE mem_byte_141 (.H(H12), .V(V7), .S(in_1), .E(in_3), .RESET(in_5), .in_6(in_6), .out_8(out_7), .op(out_208));
  MEM_BYTE mem_byte_142 (.H(H13), .V(V7), .S(in_1), .E(in_3), .RESET(in_5), .in_6(in_6), .out_8(out_7), .op(out_224));
  MEM_BYTE mem_byte_143 (.H(H14), .V(V7), .S(in_1), .E(in_3), .RESET(in_5), .in_6(in_6), .out_8(out_7), .op(out_240));
  MEM_BYTE mem_byte_144 (.H(H15), .V(V7), .S(in_1), .E(in_3), .RESET(in_5), .in_6(in_6), .out_8(out_7), .op(out_256));
  CPU_DEC_4_16 cpu_dec_4_16_2 (
    .in_1(mem_8_bits_1_out_3[3:0]), .out_13(V11), .out_14(V12), .out_15(V13), .out_16(V14), .M(V15), .L(V0),
    .out_3(V1), .out_4(V2), .out_5(V3), .out_6(V4), .out_7(V5), .out_8(V6), .out_9(V7), .out_10(V8),
    .out_11(V9), .out_12(V10));
  MEM_BYTE mem_byte_145 (.H(H0), .V(V6), .S(in_1), .E(in_3), .RESET(in_5), .in_6(in_6), .out_8(out_7), .op(out_17));
  MEM_BYTE mem_byte_146 (.H(H1), .V(V6), .S(in_1), .E(in_3), .RESET(in_5), .in_6(in_6), .out_8(out_7), .op(out_33));
  MEM_BYTE mem_byte_147 (.H(H2), .V(V6), .S(in_1), .E(in_3), .RESET(in_5), .in_6(in_6), .out_8(out_7), .op(out_49));
  MEM_BYTE mem_byte_148 (.H(H3), .V(V6), .S(in_1), .E(in_3), .RESET(in_5), .in_6(in_6), .out_8(out_7), .op(out_65));
  MEM_BYTE mem_byte_149 (.H(H4), .V(V6), .S(in_1), .E(in_3), .RESET(in_5), .in_6(in_6), .out_8(out_7), .op(out_81));
  MEM_BYTE mem_byte_150 (.H(H5), .V(V6), .S(in_1), .E(in_3), .RESET(in_5), .in_6(in_6), .out_8(out_7), .op(out_97));
  MEM_BYTE mem_byte_151 (.H(H6), .V(V6), .S(in_1), .E(in_3), .RESET(in_5), .in_6(in_6), .out_8(out_7), .op(out_113));
  MEM_BYTE mem_byte_152 (.H(H7), .V(V6), .S(in_1), .E(in_3), .RESET(in_5), .in_6(in_6), .out_8(out_7), .op(out_129));
  MEM_BYTE mem_byte_153 (.H(H8), .V(V6), .S(in_1), .E(in_3), .RESET(in_5), .in_6(in_6), .out_8(out_7), .op(out_145));
  MEM_BYTE mem_byte_154 (.H(H9), .V(V6), .S(in_1), .E(in_3), .RESET(in_5), .in_6(in_6), .out_8(out_7), .op(out_161));
  MEM_BYTE mem_byte_155 (.H(H10), .V(V6), .S(in_1), .E(in_3), .RESET(in_5), .in_6(in_6), .out_8(out_7), .op(out_177));
  MEM_BYTE mem_byte_156 (.H(H11), .V(V6), .S(in_1), .E(in_3), .RESET(in_5), .in_6(in_6), .out_8(out_7), .op(out_193));
  MEM_BYTE mem_byte_157 (.H(H12), .V(V6), .S(in_1), .E(in_3), .RESET(in_5), .in_6(in_6), .out_8(out_7), .op(out_209));
  MEM_BYTE mem_byte_158 (.H(H13), .V(V6), .S(in_1), .E(in_3), .RESET(in_5), .in_6(in_6), .out_8(out_7), .op(out_225));
  MEM_BYTE mem_byte_159 (.H(H14), .V(V6), .S(in_1), .E(in_3), .RESET(in_5), .in_6(in_6), .out_8(out_7), .op(out_241));
  MEM_BYTE mem_byte_160 (.H(H15), .V(V6), .S(in_1), .E(in_3), .RESET(in_5), .in_6(in_6), .out_8(out_7), .op(out_257));
  MEM_BYTE mem_byte_161 (.H(H0), .V(V5), .S(in_1), .E(in_3), .RESET(in_5), .in_6(in_6), .out_8(out_7), .op(out_18));
  MEM_BYTE mem_byte_162 (.H(H1), .V(V5), .S(in_1), .E(in_3), .RESET(in_5), .in_6(in_6), .out_8(out_7), .op(out_34));
  MEM_BYTE mem_byte_163 (.H(H2), .V(V5), .S(in_1), .E(in_3), .RESET(in_5), .in_6(in_6), .out_8(out_7), .op(out_50));
  MEM_BYTE mem_byte_164 (.H(H3), .V(V5), .S(in_1), .E(in_3), .RESET(in_5), .in_6(in_6), .out_8(out_7), .op(out_66));
  MEM_BYTE mem_byte_165 (.H(H4), .V(V5), .S(in_1), .E(in_3), .RESET(in_5), .in_6(in_6), .out_8(out_7), .op(out_82));
  MEM_BYTE mem_byte_166 (.H(H5), .V(V5), .S(in_1), .E(in_3), .RESET(in_5), .in_6(in_6), .out_8(out_7), .op(out_98));
  MEM_BYTE mem_byte_167 (.H(H6), .V(V5), .S(in_1), .E(in_3), .RESET(in_5), .in_6(in_6), .out_8(out_7), .op(out_114));
  MEM_BYTE mem_byte_168 (.H(H7), .V(V5), .S(in_1), .E(in_3), .RESET(in_5), .in_6(in_6), .out_8(out_7), .op(out_130));
  MEM_BYTE mem_byte_169 (.H(H8), .V(V5), .S(in_1), .E(in_3), .RESET(in_5), .in_6(in_6), .out_8(out_7), .op(out_146));
  MEM_BYTE mem_byte_170 (.H(H9), .V(V5), .S(in_1), .E(in_3), .RESET(in_5), .in_6(in_6), .out_8(out_7), .op(out_162));
  MEM_BYTE mem_byte_171 (.H(H10), .V(V5), .S(in_1), .E(in_3), .RESET(in_5), .in_6(in_6), .out_8(out_7), .op(out_178));
  MEM_BYTE mem_byte_172 (.H(H11), .V(V5), .S(in_1), .E(in_3), .RESET(in_5), .in_6(in_6), .out_8(out_7), .op(out_194));
  MEM_BYTE mem_byte_173 (.H(H12), .V(V5), .S(in_1), .E(in_3), .RESET(in_5), .in_6(in_6), .out_8(out_7), .op(out_210));
  MEM_BYTE mem_byte_174 (.H(H13), .V(V5), .S(in_1), .E(in_3), .RESET(in_5), .in_6(in_6), .out_8(out_7), .op(out_226));
  MEM_BYTE mem_byte_175 (.H(H14), .V(V5), .S(in_1), .E(in_3), .RESET(in_5), .in_6(in_6), .out_8(out_7), .op(out_242));
  MEM_BYTE mem_byte_176 (.H(H15), .V(V5), .S(in_1), .E(in_3), .RESET(in_5), .in_6(in_6), .out_8(out_7), .op(out_258));
  MEM_BYTE mem_byte_177 (.H(H0), .V(V4), .S(in_1), .E(in_3), .RESET(in_5), .in_6(in_6), .out_8(out_7), .op(out_19));
  MEM_BYTE mem_byte_178 (.H(H1), .V(V4), .S(in_1), .E(in_3), .RESET(in_5), .in_6(in_6), .out_8(out_7), .op(out_35));
  MEM_BYTE mem_byte_179 (.H(H2), .V(V4), .S(in_1), .E(in_3), .RESET(in_5), .in_6(in_6), .out_8(out_7), .op(out_51));
  MEM_BYTE mem_byte_180 (.H(H3), .V(V4), .S(in_1), .E(in_3), .RESET(in_5), .in_6(in_6), .out_8(out_7), .op(out_67));
  MEM_BYTE mem_byte_181 (.H(H4), .V(V4), .S(in_1), .E(in_3), .RESET(in_5), .in_6(in_6), .out_8(out_7), .op(out_83));
  MEM_BYTE mem_byte_182 (.H(H5), .V(V4), .S(in_1), .E(in_3), .RESET(in_5), .in_6(in_6), .out_8(out_7), .op(out_99));
  MEM_BYTE mem_byte_183 (.H(H6), .V(V4), .S(in_1), .E(in_3), .RESET(in_5), .in_6(in_6), .out_8(out_7), .op(out_115));
  MEM_BYTE mem_byte_184 (.H(H7), .V(V4), .S(in_1), .E(in_3), .RESET(in_5), .in_6(in_6), .out_8(out_7), .op(out_131));
  MEM_BYTE mem_byte_185 (.H(H8), .V(V4), .S(in_1), .E(in_3), .RESET(in_5), .in_6(in_6), .out_8(out_7), .op(out_147));
  MEM_BYTE mem_byte_186 (.H(H9), .V(V4), .S(in_1), .E(in_3), .RESET(in_5), .in_6(in_6), .out_8(out_7), .op(out_163));
  MEM_BYTE mem_byte_187 (.H(H10), .V(V4), .S(in_1), .E(in_3), .RESET(in_5), .in_6(in_6), .out_8(out_7), .op(out_179));
  MEM_BYTE mem_byte_188 (.H(H11), .V(V4), .S(in_1), .E(in_3), .RESET(in_5), .in_6(in_6), .out_8(out_7), .op(out_195));
  MEM_BYTE mem_byte_189 (.H(H12), .V(V4), .S(in_1), .E(in_3), .RESET(in_5), .in_6(in_6), .out_8(out_7), .op(out_211));
  MEM_BYTE mem_byte_190 (.H(H13), .V(V4), .S(in_1), .E(in_3), .RESET(in_5), .in_6(in_6), .out_8(out_7), .op(out_227));
  MEM_BYTE mem_byte_191 (.H(H14), .V(V4), .S(in_1), .E(in_3), .RESET(in_5), .in_6(in_6), .out_8(out_7), .op(out_243));
  MEM_BYTE mem_byte_192 (.H(H15), .V(V4), .S(in_1), .E(in_3), .RESET(in_5), .in_6(in_6), .out_8(out_7), .op(out_259));
  MEM_BYTE mem_byte_193 (.H(H0), .V(V3), .S(in_1), .E(in_3), .RESET(in_5), .in_6(in_6), .out_8(out_7), .op(out_20));
  MEM_BYTE mem_byte_194 (.H(H1), .V(V3), .S(in_1), .E(in_3), .RESET(in_5), .in_6(in_6), .out_8(out_7), .op(out_36));
  MEM_BYTE mem_byte_195 (.H(H2), .V(V3), .S(in_1), .E(in_3), .RESET(in_5), .in_6(in_6), .out_8(out_7), .op(out_52));
  MEM_BYTE mem_byte_196 (.H(H3), .V(V3), .S(in_1), .E(in_3), .RESET(in_5), .in_6(in_6), .out_8(out_7), .op(out_68));
  MEM_BYTE mem_byte_197 (.H(H4), .V(V3), .S(in_1), .E(in_3), .RESET(in_5), .in_6(in_6), .out_8(out_7), .op(out_84));
  MEM_BYTE mem_byte_198 (.H(H5), .V(V3), .S(in_1), .E(in_3), .RESET(in_5), .in_6(in_6), .out_8(out_7), .op(out_100));
  MEM_BYTE mem_byte_199 (.H(H6), .V(V3), .S(in_1), .E(in_3), .RESET(in_5), .in_6(in_6), .out_8(out_7), .op(out_116));
  MEM_BYTE mem_byte_200 (.H(H7), .V(V3), .S(in_1), .E(in_3), .RESET(in_5), .in_6(in_6), .out_8(out_7), .op(out_132));
  MEM_BYTE mem_byte_201 (.H(H8), .V(V3), .S(in_1), .E(in_3), .RESET(in_5), .in_6(in_6), .out_8(out_7), .op(out_148));
  MEM_BYTE mem_byte_202 (.H(H9), .V(V3), .S(in_1), .E(in_3), .RESET(in_5), .in_6(in_6), .out_8(out_7), .op(out_164));
  MEM_BYTE mem_byte_203 (.H(H10), .V(V3), .S(in_1), .E(in_3), .RESET(in_5), .in_6(in_6), .out_8(out_7), .op(out_180));
  MEM_BYTE mem_byte_204 (.H(H11), .V(V3), .S(in_1), .E(in_3), .RESET(in_5), .in_6(in_6), .out_8(out_7), .op(out_196));
  MEM_BYTE mem_byte_205 (.H(H12), .V(V3), .S(in_1), .E(in_3), .RESET(in_5), .in_6(in_6), .out_8(out_7), .op(out_212));
  MEM_BYTE mem_byte_206 (.H(H13), .V(V3), .S(in_1), .E(in_3), .RESET(in_5), .in_6(in_6), .out_8(out_7), .op(out_228));
  MEM_BYTE mem_byte_207 (.H(H14), .V(V3), .S(in_1), .E(in_3), .RESET(in_5), .in_6(in_6), .out_8(out_7), .op(out_244));
  MEM_BYTE mem_byte_208 (.H(H15), .V(V3), .S(in_1), .E(in_3), .RESET(in_5), .in_6(in_6), .out_8(out_7), .op(out_260));
  MEM_BYTE mem_byte_209 (.H(H0), .V(V2), .S(in_1), .E(in_3), .RESET(in_5), .in_6(in_6), .out_8(out_7), .op(out_21));
  MEM_BYTE mem_byte_210 (.H(H1), .V(V2), .S(in_1), .E(in_3), .RESET(in_5), .in_6(in_6), .out_8(out_7), .op(out_37));
  MEM_BYTE mem_byte_211 (.H(H2), .V(V2), .S(in_1), .E(in_3), .RESET(in_5), .in_6(in_6), .out_8(out_7), .op(out_53));
  MEM_BYTE mem_byte_212 (.H(H3), .V(V2), .S(in_1), .E(in_3), .RESET(in_5), .in_6(in_6), .out_8(out_7), .op(out_69));
  MEM_BYTE mem_byte_213 (.H(H4), .V(V2), .S(in_1), .E(in_3), .RESET(in_5), .in_6(in_6), .out_8(out_7), .op(out_85));
  MEM_BYTE mem_byte_214 (.H(H5), .V(V2), .S(in_1), .E(in_3), .RESET(in_5), .in_6(in_6), .out_8(out_7), .op(out_101));
  MEM_BYTE mem_byte_215 (.H(H6), .V(V2), .S(in_1), .E(in_3), .RESET(in_5), .in_6(in_6), .out_8(out_7), .op(out_117));
  MEM_BYTE mem_byte_216 (.H(H7), .V(V2), .S(in_1), .E(in_3), .RESET(in_5), .in_6(in_6), .out_8(out_7), .op(out_133));
  MEM_BYTE mem_byte_217 (.H(H8), .V(V2), .S(in_1), .E(in_3), .RESET(in_5), .in_6(in_6), .out_8(out_7), .op(out_149));
  MEM_BYTE mem_byte_218 (.H(H9), .V(V2), .S(in_1), .E(in_3), .RESET(in_5), .in_6(in_6), .out_8(out_7), .op(out_165));
  MEM_BYTE mem_byte_219 (.H(H10), .V(V2), .S(in_1), .E(in_3), .RESET(in_5), .in_6(in_6), .out_8(out_7), .op(out_181));
  MEM_BYTE mem_byte_220 (.H(H11), .V(V2), .S(in_1), .E(in_3), .RESET(in_5), .in_6(in_6), .out_8(out_7), .op(out_197));
  MEM_BYTE mem_byte_221 (.H(H12), .V(V2), .S(in_1), .E(in_3), .RESET(in_5), .in_6(in_6), .out_8(out_7), .op(out_213));
  MEM_BYTE mem_byte_222 (.H(H13), .V(V2), .S(in_1), .E(in_3), .RESET(in_5), .in_6(in_6), .out_8(out_7), .op(out_229));
  MEM_BYTE mem_byte_223 (.H(H14), .V(V2), .S(in_1), .E(in_3), .RESET(in_5), .in_6(in_6), .out_8(out_7), .op(out_245));
  MEM_BYTE mem_byte_224 (.H(H15), .V(V2), .S(in_1), .E(in_3), .RESET(in_5), .in_6(in_6), .out_8(out_7), .op(out_261));
  MEM_BYTE mem_byte_225 (.H(H0), .V(V1), .S(in_1), .E(in_3), .RESET(in_5), .in_6(in_6), .out_8(out_7), .op(out_22));
  MEM_BYTE mem_byte_226 (.H(H1), .V(V1), .S(in_1), .E(in_3), .RESET(in_5), .in_6(in_6), .out_8(out_7), .op(out_38));
  MEM_BYTE mem_byte_227 (.H(H2), .V(V1), .S(in_1), .E(in_3), .RESET(in_5), .in_6(in_6), .out_8(out_7), .op(out_54));
  MEM_BYTE mem_byte_228 (.H(H3), .V(V1), .S(in_1), .E(in_3), .RESET(in_5), .in_6(in_6), .out_8(out_7), .op(out_70));
  MEM_BYTE mem_byte_229 (.H(H4), .V(V1), .S(in_1), .E(in_3), .RESET(in_5), .in_6(in_6), .out_8(out_7), .op(out_86));
  MEM_BYTE mem_byte_230 (.H(H5), .V(V1), .S(in_1), .E(in_3), .RESET(in_5), .in_6(in_6), .out_8(out_7), .op(out_102));
  MEM_BYTE mem_byte_231 (.H(H6), .V(V1), .S(in_1), .E(in_3), .RESET(in_5), .in_6(in_6), .out_8(out_7), .op(out_118));
  MEM_BYTE mem_byte_232 (.H(H7), .V(V1), .S(in_1), .E(in_3), .RESET(in_5), .in_6(in_6), .out_8(out_7), .op(out_134));
  MEM_BYTE mem_byte_233 (.H(H8), .V(V1), .S(in_1), .E(in_3), .RESET(in_5), .in_6(in_6), .out_8(out_7), .op(out_150));
  MEM_BYTE mem_byte_234 (.H(H9), .V(V1), .S(in_1), .E(in_3), .RESET(in_5), .in_6(in_6), .out_8(out_7), .op(out_166));
  MEM_BYTE mem_byte_235 (.H(H10), .V(V1), .S(in_1), .E(in_3), .RESET(in_5), .in_6(in_6), .out_8(out_7), .op(out_182));
  MEM_BYTE mem_byte_236 (.H(H11), .V(V1), .S(in_1), .E(in_3), .RESET(in_5), .in_6(in_6), .out_8(out_7), .op(out_198));
  MEM_BYTE mem_byte_237 (.H(H12), .V(V1), .S(in_1), .E(in_3), .RESET(in_5), .in_6(in_6), .out_8(out_7), .op(out_214));
  MEM_BYTE mem_byte_238 (.H(H13), .V(V1), .S(in_1), .E(in_3), .RESET(in_5), .in_6(in_6), .out_8(out_7), .op(out_230));
  MEM_BYTE mem_byte_239 (.H(H14), .V(V1), .S(in_1), .E(in_3), .RESET(in_5), .in_6(in_6), .out_8(out_7), .op(out_246));
  MEM_BYTE mem_byte_240 (.H(H15), .V(V1), .S(in_1), .E(in_3), .RESET(in_5), .in_6(in_6), .out_8(out_7), .op(out_262));
  MEM_BYTE mem_byte_241 (.H(H0), .V(V0), .S(in_1), .E(in_3), .RESET(in_5), .in_6(in_6), .out_8(out_7), .op(out_23));
  MEM_BYTE mem_byte_242 (.H(H1), .V(V0), .S(in_1), .E(in_3), .RESET(in_5), .in_6(in_6), .out_8(out_7), .op(out_39));
  MEM_BYTE mem_byte_243 (.H(H2), .V(V0), .S(in_1), .E(in_3), .RESET(in_5), .in_6(in_6), .out_8(out_7), .op(out_55));
  MEM_BYTE mem_byte_244 (.H(H3), .V(V0), .S(in_1), .E(in_3), .RESET(in_5), .in_6(in_6), .out_8(out_7), .op(out_71));
  MEM_BYTE mem_byte_245 (.H(H4), .V(V0), .S(in_1), .E(in_3), .RESET(in_5), .in_6(in_6), .out_8(out_7), .op(out_87));
  MEM_BYTE mem_byte_246 (.H(H5), .V(V0), .S(in_1), .E(in_3), .RESET(in_5), .in_6(in_6), .out_8(out_7), .op(out_103));
  MEM_BYTE mem_byte_247 (.H(H6), .V(V0), .S(in_1), .E(in_3), .RESET(in_5), .in_6(in_6), .out_8(out_7), .op(out_119));
  MEM_BYTE mem_byte_248 (.H(H7), .V(V0), .S(in_1), .E(in_3), .RESET(in_5), .in_6(in_6), .out_8(out_7), .op(out_135));
  MEM_BYTE mem_byte_249 (.H(H8), .V(V0), .S(in_1), .E(in_3), .RESET(in_5), .in_6(in_6), .out_8(out_7), .op(out_151));
  MEM_BYTE mem_byte_250 (.H(H9), .V(V0), .S(in_1), .E(in_3), .RESET(in_5), .in_6(in_6), .out_8(out_7), .op(out_167));
  MEM_BYTE mem_byte_251 (.H(H10), .V(V0), .S(in_1), .E(in_3), .RESET(in_5), .in_6(in_6), .out_8(out_7), .op(out_183));
  MEM_BYTE mem_byte_252 (.H(H11), .V(V0), .S(in_1), .E(in_3), .RESET(in_5), .in_6(in_6), .out_8(out_7), .op(out_199));
  MEM_BYTE mem_byte_253 (.H(H12), .V(V0), .S(in_1), .E(in_3), .RESET(in_5), .in_6(in_6), .out_8(out_7), .op(out_215));
  MEM_BYTE mem_byte_254 (.H(H13), .V(V0), .S(in_1), .E(in_3), .RESET(in_5), .in_6(in_6), .out_8(out_7), .op(out_231));
  MEM_BYTE mem_byte_255 (.H(H14), .V(V0), .S(in_1), .E(in_3), .RESET(in_5), .in_6(in_6), .out_8(out_7), .op(out_247));
  MEM_BYTE mem_byte_256 (.H(H15), .V(V0), .S(in_1), .E(in_3), .RESET(in_5), .in_6(in_6), .out_8(out_7), .op(out_263));

  // Other names for the same wires on the sheet: DIN[7:0] = in_6; DOUT[7:0] = out_7; E = in_3; RST = in_5; S = in_1

  // Notes on the sheet:
  //   ADRESS
endmodule

module MEM_8_BITS (
  input  [7:0] in_1,
  input  s,
  output [7:0] out_3
);

  MEM_LATCH mem_latch_1 (.in_2(s), .in_1(in_1[0]), .out_3(out_3[0]));
  MEM_LATCH mem_latch_2 (.in_2(s), .in_1(in_1[1]), .out_3(out_3[1]));
  MEM_LATCH mem_latch_3 (.in_2(s), .in_1(in_1[2]), .out_3(out_3[2]));
  MEM_LATCH mem_latch_4 (.in_2(s), .in_1(in_1[3]), .out_3(out_3[3]));
  MEM_LATCH mem_latch_5 (.in_2(s), .in_1(in_1[4]), .out_3(out_3[4]));
  MEM_LATCH mem_latch_6 (.in_2(s), .in_1(in_1[5]), .out_3(out_3[5]));
  MEM_LATCH mem_latch_7 (.in_2(s), .in_1(in_1[6]), .out_3(out_3[6]));
  MEM_LATCH mem_latch_8 (.in_2(s), .in_1(in_1[7]), .out_3(out_3[7]));

  // Notes on the sheet:
  //   in_1: pull=down
  //   s: pull=down
  //   out_3: pull=down
endmodule

module MEM_LATCH (
  input  in_1,
  input  in_2,
  output out_3
);

  wire nand_1_out, nand_2_out, nand_4_out;

  nand nand_1 (nand_1_out, in_1, in_2);
  nand nand_2 (nand_2_out, nand_1_out, in_2);
  nand nand_3 (out_3, nand_1_out, nand_4_out);
  nand nand_4 (nand_4_out, out_3, nand_2_out);

  // Notes on the sheet:
  //   in_2: pull=down
  //   in_1: pull=down
endmodule

module ALU (
  input  [7:0] in_1,
  input  [7:0] in_2,
  input  in_3,
  input  in_4,
  input  in_5,
  input  in_6,
  output larger,
  output [7:0] out_8,
  output equal,
  output zero,
  output carry_out
);

  wire alu_adder_8_1_out_5, alu_shift_left_1_out_4, alu_shift_right_1_shift_out, and_1_out, and_2_out,
       and_3_out;
  wire [7:0] alu_adder_8_1_out_4, alu_and_1_out_3, alu_dec_3_8_1_o, alu_le_comp_8_1_out_3, alu_not_1_out_2,
       alu_or_1_out_3, alu_shift_left_1_o, alu_shift_right_1_o;

  ALU_LE_COMP_8 alu_le_comp_8_1 (.a(in_1), .b(in_2), .equal(equal), .larger(larger), .out_3(alu_le_comp_8_1_out_3));
  ALU_OR alu_or_1 (.in_1(in_1), .in_2(in_2), .out_3(alu_or_1_out_3));
  ALU_AND alu_and_1 (.in_1(in_1), .in_2(in_2), .out_3(alu_and_1_out_3));
  ALU_NOT alu_not_1 (.i(in_1), .out_2(alu_not_1_out_2));
  ALU_SHIFT_LEFT alu_shift_left_1 (
    .in_2(in_1), .SHIFT_IN(in_3), .out_4(alu_shift_left_1_out_4), .o(alu_shift_left_1_o));
  ALU_ADDER_8 alu_adder_8_1 (
    .in_1(in_1), .in_2(in_2), .in_3(in_3), .out_4(alu_adder_8_1_out_4), .out_5(alu_adder_8_1_out_5));
  ALU_SHIFT_RIGHT alu_shift_right_1 (
    .in_1(in_1), .in_2(in_3), .SHIFT_OUT(alu_shift_right_1_shift_out), .o(alu_shift_right_1_o));
  MEM_ENABLE_8 mem_enable_8_1 (.in_1(alu_le_comp_8_1_out_3), .in_2(alu_dec_3_8_1_o[6]), .out_3(out_8));
  MEM_ENABLE_8 mem_enable_8_2 (.in_1(alu_or_1_out_3), .in_2(alu_dec_3_8_1_o[5]), .out_3(out_8));
  MEM_ENABLE_8 mem_enable_8_3 (.in_1(alu_and_1_out_3), .in_2(alu_dec_3_8_1_o[4]), .out_3(out_8));
  MEM_ENABLE_8 mem_enable_8_4 (.in_1(alu_not_1_out_2), .in_2(alu_dec_3_8_1_o[3]), .out_3(out_8));
  MEM_ENABLE_8 mem_enable_8_5 (.in_1(alu_shift_left_1_o), .in_2(alu_dec_3_8_1_o[2]), .out_3(out_8));
  MEM_ENABLE_8 mem_enable_8_6 (.in_1(alu_shift_right_1_o), .in_2(alu_dec_3_8_1_o[1]), .out_3(out_8));
  ALU_DEC_3_8 alu_dec_3_8_1 (.c(in_6), .b(in_5), .a(in_4), .o(alu_dec_3_8_1_o));
  MEM_ENABLE_8 mem_enable_8_7 (.in_1(alu_adder_8_1_out_4), .in_2(alu_dec_3_8_1_o[0]), .out_3(out_8));
  and and_1 (and_1_out, alu_shift_left_1_out_4, alu_dec_3_8_1_o[2]);
  and and_2 (and_2_out, alu_shift_right_1_shift_out, alu_dec_3_8_1_o[1]);
  and and_3 (and_3_out, alu_adder_8_1_out_5, alu_dec_3_8_1_o[0]);
  assign carry_out = alu_dec_3_8_1_o[2] ? and_1_out : 1'bz;  // Controlled_Buffer controlled_buffer_1
  assign carry_out = alu_dec_3_8_1_o[1] ? and_2_out : 1'bz;  // Controlled_Buffer controlled_buffer_2
  assign carry_out = alu_dec_3_8_1_o[0] ? and_3_out : 1'bz;  // Controlled_Buffer controlled_buffer_3
  ALU_ZERO alu_zero_1 (.i(out_8), .o(zero));
endmodule

module FULLADDER (
  input  A,
  input  B,
  input  CI,
  output SUM,
  output CARRY_OUT
);

  wire and_1_out, and_2_out, xor_1_out;

  xor xor_1 (xor_1_out, A, B);
  and and_1 (and_1_out, A, B);
  and and_2 (and_2_out, CI, xor_1_out);
  xor xor_2 (SUM, xor_1_out, CI);
  or or_1 (CARRY_OUT, and_2_out, and_1_out);
endmodule

module ALU_ADDER_8 (
  input  [7:0] in_1,
  input  [7:0] in_2,
  input  in_3,
  output [7:0] out_4,
  output out_5
);

  wire fulladder_1_carry_out, fulladder_2_carry_out, fulladder_3_carry_out, fulladder_4_carry_out,
       fulladder_5_carry_out, fulladder_6_carry_out, fulladder_7_carry_out;

  FULLADDER fulladder_1 (.A(in_1[0]), .B(in_2[0]), .CI(in_3), .SUM(out_4[0]), .CARRY_OUT(fulladder_1_carry_out));
  FULLADDER fulladder_2 (
    .A(in_1[1]), .B(in_2[1]), .CI(fulladder_1_carry_out), .SUM(out_4[1]), .CARRY_OUT(fulladder_2_carry_out));
  FULLADDER fulladder_3 (
    .A(in_1[2]), .B(in_2[2]), .CI(fulladder_2_carry_out), .SUM(out_4[2]), .CARRY_OUT(fulladder_3_carry_out));
  FULLADDER fulladder_4 (
    .A(in_1[3]), .B(in_2[3]), .CI(fulladder_3_carry_out), .SUM(out_4[3]), .CARRY_OUT(fulladder_4_carry_out));
  FULLADDER fulladder_5 (
    .A(in_1[4]), .B(in_2[4]), .CI(fulladder_4_carry_out), .SUM(out_4[4]), .CARRY_OUT(fulladder_5_carry_out));
  FULLADDER fulladder_6 (
    .A(in_1[5]), .B(in_2[5]), .CI(fulladder_5_carry_out), .SUM(out_4[5]), .CARRY_OUT(fulladder_6_carry_out));
  FULLADDER fulladder_7 (
    .A(in_1[6]), .B(in_2[6]), .CI(fulladder_6_carry_out), .SUM(out_4[6]), .CARRY_OUT(fulladder_7_carry_out));
  FULLADDER fulladder_8 (.A(in_1[7]), .B(in_2[7]), .CI(fulladder_7_carry_out), .SUM(out_4[7]), .CARRY_OUT(out_5));
endmodule

module ALU_SHIFT_RIGHT (
  input  [7:0] in_1,
  input  in_2,
  output SHIFT_OUT,
  output [7:0] o
);

  wire [7:1] mem_register_8_1_l_0_c0844130;

  MEM_REGISTER_8 mem_register_8_1 (
    .i(in_1), .s(1'b1), .e(1'b1), .L_0_c0844130({mem_register_8_1_l_0_c0844130, SHIFT_OUT}));  // open: REG
  MEM_REGISTER_8 mem_register_8_2 (
    .i({in_2, mem_register_8_1_l_0_c0844130}), .s(1'b1), .e(1'b1), .L_0_c0844130(o));  // open: REG

  // Notes on the sheet:
  //   SHIFT IN
endmodule

module MEM_REGISTER_8 (
  input  [7:0] i,
  input  s,
  input  e,
  output [7:0] REG,
  output [7:0] L_0_c0844130
);

  wire [7:0] mem_enable_8_1_out_3;

  MEM_8_BITS mem_8_bits_1 (.in_1(i), .s(s), .out_3(REG));
  MEM_ENABLE_8 mem_enable_8_1 (.in_1(REG), .in_2(e), .out_3(mem_enable_8_1_out_3));
  assign L_0_c0844130 = e ? mem_enable_8_1_out_3 : 8'bz;  // Controlled_Buffer controlled_buffer_1

  // Notes on the sheet:
  //   i: pull=down
  //   s: pull=down
  //   e: pull=down
  //   L_0_c0844130: pull=down
endmodule

module MEM_ENABLE_8 (
  input  [7:0] in_1,
  input  in_2,
  output [7:0] out_3
);

  wire and_1_out, and_2_out, and_3_out, and_4_out, and_5_out, and_6_out, and_7_out, and_8_out;

  and and_1 (and_1_out, in_1[0], in_2);
  assign out_3[0] = in_2 ? and_1_out : 1'bz;  // Controlled_Buffer controlled_buffer_1
  and and_2 (and_2_out, in_1[1], in_2);
  assign out_3[1] = in_2 ? and_2_out : 1'bz;  // Controlled_Buffer controlled_buffer_2
  and and_3 (and_3_out, in_1[2], in_2);
  assign out_3[2] = in_2 ? and_3_out : 1'bz;  // Controlled_Buffer controlled_buffer_3
  and and_4 (and_4_out, in_1[3], in_2);
  assign out_3[3] = in_2 ? and_4_out : 1'bz;  // Controlled_Buffer controlled_buffer_4
  and and_5 (and_5_out, in_1[4], in_2);
  assign out_3[4] = in_2 ? and_5_out : 1'bz;  // Controlled_Buffer controlled_buffer_5
  and and_6 (and_6_out, in_1[5], in_2);
  assign out_3[5] = in_2 ? and_6_out : 1'bz;  // Controlled_Buffer controlled_buffer_6
  and and_7 (and_7_out, in_1[6], in_2);
  assign out_3[6] = in_2 ? and_7_out : 1'bz;  // Controlled_Buffer controlled_buffer_7
  and and_8 (and_8_out, in_1[7], in_2);
  assign out_3[7] = in_2 ? and_8_out : 1'bz;  // Controlled_Buffer controlled_buffer_8
endmodule

module ALU_SHIFT_LEFT (
  input  SHIFT_IN,
  input  [7:0] in_2,
  output [7:0] o,
  output out_4
);

  wire [6:0] mem_register_8_1_l_0_c0844130;

  MEM_REGISTER_8 mem_register_8_1 (
    .i(in_2), .s(1'b1), .e(1'b1), .L_0_c0844130({out_4, mem_register_8_1_l_0_c0844130}));  // open: REG
  MEM_REGISTER_8 mem_register_8_2 (
    .i({mem_register_8_1_l_0_c0844130, SHIFT_IN}), .s(1'b1), .e(1'b1), .L_0_c0844130(o));  // open: REG

  // Notes on the sheet:
  //   SHIFT OUT
endmodule

module ALU_NOT (
  input  [7:0] i,
  output [7:0] out_2
);

  not not_1 (out_2[0], i[0]);
  not not_2 (out_2[1], i[1]);
  not not_3 (out_2[2], i[2]);
  not not_4 (out_2[3], i[3]);
  not not_5 (out_2[4], i[4]);
  not not_6 (out_2[5], i[5]);
  not not_7 (out_2[6], i[6]);
  not not_8 (out_2[7], i[7]);
endmodule

module ALU_AND (
  input  [7:0] in_1,
  input  [7:0] in_2,
  output [7:0] out_3
);

  and and_1 (out_3[0], in_1[0], in_2[0]);
  and and_2 (out_3[1], in_1[1], in_2[1]);
  and and_3 (out_3[2], in_1[2], in_2[2]);
  and and_4 (out_3[3], in_1[3], in_2[3]);
  and and_5 (out_3[4], in_1[4], in_2[4]);
  and and_6 (out_3[5], in_1[5], in_2[5]);
  and and_7 (out_3[6], in_1[6], in_2[6]);
  and and_8 (out_3[7], in_1[7], in_2[7]);
endmodule

module ALU_OR (
  input  [7:0] in_1,
  input  [7:0] in_2,
  output [7:0] out_3
);

  or or_1 (out_3[0], in_1[0], in_2[0]);
  or or_2 (out_3[1], in_1[1], in_2[1]);
  or or_3 (out_3[2], in_1[2], in_2[2]);
  or or_4 (out_3[3], in_1[3], in_2[3]);
  or or_5 (out_3[4], in_1[4], in_2[4]);
  or or_6 (out_3[5], in_1[5], in_2[5]);
  or or_7 (out_3[6], in_1[6], in_2[6]);
  or or_8 (out_3[7], in_1[7], in_2[7]);
endmodule

module ALU_LE_COMP (
  input  in_1,
  input  A_LARGER,
  input  A,
  input  B,
  output C,
  output EQUAL,
  output A_LARGE
);

  wire and_2_out, not_1_out;

  ALU_XOR_1 alu_xor_1_1 (.a(A), .b(B), .o(C));
  not not_1 (not_1_out, C);
  and and_1 (EQUAL, not_1_out, in_1);
  and and_2 (and_2_out, in_1, A, C);
  or or_1 (A_LARGE, and_2_out, A_LARGER);

  // Notes on the sheet:
  //   ABOVE EQUAL
endmodule

module ALU_LE_COMP_8 (
  input  [7:0] a,
  input  [7:0] b,
  output [7:0] out_3,
  output larger,
  output equal
);

  wire alu_le_comp_1_a_large, alu_le_comp_1_equal, alu_le_comp_2_a_large, alu_le_comp_2_equal,
       alu_le_comp_3_a_large, alu_le_comp_3_equal, alu_le_comp_4_a_large, alu_le_comp_4_equal,
       alu_le_comp_5_a_large, alu_le_comp_5_equal, alu_le_comp_6_a_large, alu_le_comp_6_equal,
       alu_le_comp_7_a_large, alu_le_comp_7_equal;

  ALU_LE_COMP alu_le_comp_1 (
    .A(a[7]), .B(b[7]), .in_1(1'b1), .A_LARGER(1'b0), .EQUAL(alu_le_comp_1_equal),
    .A_LARGE(alu_le_comp_1_a_large), .C(out_3[7]));
  ALU_LE_COMP alu_le_comp_2 (
    .A(a[6]), .B(b[6]), .in_1(alu_le_comp_1_equal), .A_LARGER(alu_le_comp_1_a_large),
    .EQUAL(alu_le_comp_2_equal), .A_LARGE(alu_le_comp_2_a_large), .C(out_3[6]));
  ALU_LE_COMP alu_le_comp_3 (
    .A(a[5]), .B(b[5]), .in_1(alu_le_comp_2_equal), .A_LARGER(alu_le_comp_2_a_large),
    .EQUAL(alu_le_comp_3_equal), .A_LARGE(alu_le_comp_3_a_large), .C(out_3[5]));
  ALU_LE_COMP alu_le_comp_4 (
    .A(a[4]), .B(b[4]), .in_1(alu_le_comp_3_equal), .A_LARGER(alu_le_comp_3_a_large),
    .EQUAL(alu_le_comp_4_equal), .A_LARGE(alu_le_comp_4_a_large), .C(out_3[4]));
  ALU_LE_COMP alu_le_comp_5 (
    .A(a[3]), .B(b[3]), .in_1(alu_le_comp_4_equal), .A_LARGER(alu_le_comp_4_a_large),
    .EQUAL(alu_le_comp_5_equal), .A_LARGE(alu_le_comp_5_a_large), .C(out_3[3]));
  ALU_LE_COMP alu_le_comp_6 (
    .A(a[2]), .B(b[2]), .in_1(alu_le_comp_5_equal), .A_LARGER(alu_le_comp_5_a_large),
    .EQUAL(alu_le_comp_6_equal), .A_LARGE(alu_le_comp_6_a_large), .C(out_3[2]));
  ALU_LE_COMP alu_le_comp_7 (
    .A(a[1]), .B(b[1]), .in_1(alu_le_comp_6_equal), .A_LARGER(alu_le_comp_6_a_large),
    .EQUAL(alu_le_comp_7_equal), .A_LARGE(alu_le_comp_7_a_large), .C(out_3[1]));
  ALU_LE_COMP alu_le_comp_8 (
    .A(a[0]), .B(b[0]), .in_1(alu_le_comp_7_equal), .A_LARGER(alu_le_comp_7_a_large), .EQUAL(equal),
    .A_LARGE(larger), .C(out_3[0]));
endmodule

module ALU_XOR_1 (
  input  a,
  input  b,
  output o
);

  wire nand_1_out, nand_2_out, not_1_out, not_2_out;

  not not_1 (not_1_out, a);
  not not_2 (not_2_out, b);
  nand nand_1 (nand_1_out, not_1_out, b);
  nand nand_2 (nand_2_out, a, not_2_out);
  nand nand_3 (o, nand_1_out, nand_2_out);
endmodule

module ALU_DEC_3_8 (
  input  c,
  input  b,
  input  a,
  output [7:0] o
);

  wire not_1_out, not_2_out, not_3_out;

  not not_1 (not_1_out, a);
  not not_2 (not_2_out, b);
  not not_3 (not_3_out, c);
  and and_1 (o[0], not_3_out, not_2_out, not_1_out);
  and and_2 (o[1], not_3_out, not_2_out, a);
  and and_3 (o[2], not_3_out, b, not_1_out);
  and and_4 (o[3], not_3_out, b, a);
  and and_5 (o[4], c, not_2_out, not_1_out);
  and and_6 (o[5], c, not_2_out, a);
  and and_7 (o[6], c, b, not_1_out);
  and and_8 (o[7], c, b, a);

  // Notes on the sheet:
  //   c: pull=down
  //   b: pull=down
  //   a: pull=down
  //   o: pull=down
  //   msb
  //   lsb
endmodule

module ALU_ZERO (
  input  [7:0] i,
  output o
);

  wire or_1_out;

  or or_1 (or_1_out, i[0], i[1], i[2], i[3], i[4], i[5], i[6], i[7]);
  not not_1 (o, or_1_out);
endmodule

module CPU_CLOCK (
  input  CLKIN,
  output CLK,
  output CLKS,
  output CLKE
);

  wire j_k_ff_1_qn, nand_1_out;

  J_K_Flip_Flop j_k_ff_1 (.J(1'b1), .K(1'b1), .clk(CLKIN), .Q(CLK), .Qn(j_k_ff_1_qn));  // open: preset, reset
  nand nand_1 (nand_1_out, CLKIN, CLK);
  nand nand_2 (CLKE, j_k_ff_1_qn, CLKIN);
  not not_1 (CLKS, nand_1_out);
endmodule

module CONTROL_UNIT (
  input  in_1,
  input  in_2,
  input  in_3,
  input  [7:0] in_4,
  output BUS_1,
  output out_6,
  output RAM_E,
  output out_8,
  output ACC_E,
  output RAM_S,
  output out_11,
  output out_12,
  output R0_S,
  output R0_E,
  output R1_S,
  output R1_E,
  output R2_S,
  output R2_E,
  output R3_S,
  output R3_E,
  output IR_S,
  output IAR_S
);

  wire cntrl_u_stepper_1_out_4, cntrl_u_stepper_1_out_5, cntrl_u_stepper_1_out_8, cntrl_u_stepper_1_out_9;

  and and_1 (RAM_E, in_3, cntrl_u_stepper_1_out_4);
  and and_2 (ACC_E, in_3, cntrl_u_stepper_1_out_5);
  and and_3 (out_11, in_3, BUS_1);
  and and_4 (R0_E, in_3, 1'b0);
  and and_5 (R1_E, in_3, 1'b0);
  and and_6 (R2_E, in_3, 1'b0);
  and and_7 (R3_E, in_3, 1'b0);
  CNTRL_U_STEPPER cntrl_u_stepper_1 (
    .in_2(in_2), .in_1(cntrl_u_stepper_1_out_9), .out_5(cntrl_u_stepper_1_out_5),
    .out_8(cntrl_u_stepper_1_out_8), .out_9(cntrl_u_stepper_1_out_9), .out_3(BUS_1),
    .out_4(cntrl_u_stepper_1_out_4));  // open: out_6, out_7
  and and_8 (out_6, in_1, BUS_1);
  and and_9 (out_8, in_1, BUS_1);
  and and_10 (RAM_S, in_1, 1'b0);
  and and_11 (out_12, in_1, 1'b0);
  and and_12 (R0_S, in_1, 1'b0);
  and and_13 (R1_S, in_1, 1'b0);
  and and_14 (R2_S, in_1, 1'b0);
  and and_15 (R3_S, in_1, cntrl_u_stepper_1_out_8);
  and and_16 (IR_S, in_1, cntrl_u_stepper_1_out_4);
  and and_17 (IAR_S, in_1, cntrl_u_stepper_1_out_5);

  // Notes on the sheet:
  //   IAR_E
  //   CLKS
  //   CLK
  //   CLKE
  //   IR_IN
  //   MAR_S
  //   ACC_S
  //   TMP_S
endmodule

module CNTRL_U_STEPPER (
  input  in_1,
  input  in_2,
  output out_3,
  output out_4,
  output out_5,
  output out_6,
  output out_7,
  output out_8,
  output out_9
);

  wire mem_latch_1_out_3, mem_latch_2_out_3, mem_latch_3_out_3, mem_latch_4_out_3, mem_latch_5_out_3,
       mem_latch_6_out_3, mem_latch_7_out_3, mem_latch_8_out_3, mem_latch_9_out_3, mem_latch_10_out_3,
       mem_latch_11_out_3, not_1_out, not_2_out, not_3_out, not_4_out, not_5_out, not_6_out, not_7_out,
       not_8_out, or_1_out, or_2_out;

  not not_1 (not_1_out, in_2);
  not not_2 (not_2_out, in_1);
  or or_1 (or_1_out, in_1, in_2);
  or or_2 (or_2_out, in_1, not_1_out);
  or or_3 (out_3, in_1, not_3_out);
  not not_3 (not_3_out, mem_latch_2_out_3);
  MEM_LATCH mem_latch_1 (.in_2(or_1_out), .in_1(not_2_out), .out_3(mem_latch_1_out_3));
  MEM_LATCH mem_latch_2 (.in_2(or_2_out), .in_1(mem_latch_1_out_3), .out_3(mem_latch_2_out_3));
  and and_1 (out_4, mem_latch_2_out_3, not_4_out);
  not not_4 (not_4_out, mem_latch_4_out_3);
  MEM_LATCH mem_latch_3 (.in_2(or_1_out), .in_1(mem_latch_2_out_3), .out_3(mem_latch_3_out_3));
  MEM_LATCH mem_latch_4 (.in_2(or_2_out), .in_1(mem_latch_3_out_3), .out_3(mem_latch_4_out_3));
  and and_2 (out_5, mem_latch_4_out_3, not_5_out);
  MEM_LATCH mem_latch_5 (.in_2(or_1_out), .in_1(mem_latch_4_out_3), .out_3(mem_latch_5_out_3));
  not not_5 (not_5_out, mem_latch_6_out_3);
  MEM_LATCH mem_latch_6 (.in_2(or_2_out), .in_1(mem_latch_5_out_3), .out_3(mem_latch_6_out_3));
  and and_3 (out_6, mem_latch_6_out_3, not_6_out);
  MEM_LATCH mem_latch_7 (.in_2(or_1_out), .in_1(mem_latch_6_out_3), .out_3(mem_latch_7_out_3));
  not not_6 (not_6_out, mem_latch_8_out_3);
  MEM_LATCH mem_latch_8 (.in_2(or_2_out), .in_1(mem_latch_7_out_3), .out_3(mem_latch_8_out_3));
  and and_4 (out_7, mem_latch_8_out_3, not_7_out);
  not not_7 (not_7_out, mem_latch_10_out_3);
  MEM_LATCH mem_latch_9 (.in_2(or_1_out), .in_1(mem_latch_8_out_3), .out_3(mem_latch_9_out_3));
  MEM_LATCH mem_latch_10 (.in_2(or_2_out), .in_1(mem_latch_9_out_3), .out_3(mem_latch_10_out_3));
  and and_5 (out_8, mem_latch_10_out_3, not_8_out);
  MEM_LATCH mem_latch_11 (.in_2(or_1_out), .in_1(mem_latch_10_out_3), .out_3(mem_latch_11_out_3));
  not not_8 (not_8_out, out_9);
  MEM_LATCH mem_latch_12 (.in_2(or_2_out), .in_1(mem_latch_11_out_3), .out_3(out_9));
endmodule

module CPU_TEMP (
  input  [7:0] i,
  input  s,
  output [7:0] o
);

  wire [7:0] controlled_buffer_1_out;

  assign controlled_buffer_1_out = s ? i : 8'bz;  // Controlled_Buffer controlled_buffer_1
  MEM_8_BITS mem_8_bits_1 (.in_1(controlled_buffer_1_out), .s(s), .out_3(o));

  // Notes on the sheet:
  //   i: pull=down
  //   s: pull=down
  //   o: pull=down
endmodule

module CPU_BUS_1 (
  input  [7:0] i,
  input  bus_1_a6cd2c94,
  output [7:0] o
);

  wire not_1_out;

  and and_1 (o[7], i[7], not_1_out);
  and and_2 (o[6], i[6], not_1_out);
  and and_3 (o[5], i[5], not_1_out);
  and and_4 (o[4], i[4], not_1_out);
  and and_5 (o[3], i[3], not_1_out);
  and and_6 (o[2], i[2], not_1_out);
  and and_7 (o[1], i[1], not_1_out);
  not not_1 (not_1_out, bus_1_a6cd2c94);
  or or_1 (o[0], i[0], bus_1_a6cd2c94);

  // Notes on the sheet:
  //   bus_1_a6cd2c94: pull=down
  //   i: pull=down
  //   o: pull=down
endmodule

module CPU_REG (
  input  [7:0] i,
  input  s,
  input  e,
  output [7:0] \reg ,
  output [7:0] o
);

  MEM_REGISTER_8 mem_register_8_1 (.i(i), .s(s), .e(e), .REG(\reg ), .L_0_c0844130(o));

  // Notes on the sheet:
  //   i: pull=down
  //   s: pull=down
  //   e: pull=down
  //   o: pull=down
endmodule

module CPU_ACCUM (
  input  [7:0] i,
  input  s,
  input  e,
  output [7:0] ACC,
  output [7:0] o
);

  MEM_REGISTER_8 mem_register_8_1 (.i(i), .s(s), .e(e), .REG(ACC), .L_0_c0844130(o));

  // Notes on the sheet:
  //   i: pull=down
  //   s: pull=down
  //   e: pull=down
  //   o: pull=down
endmodule

module CPU_IR (
  input  [7:0] i,
  input  s,
  output [7:0] o
);

  MEM_8_BITS mem_8_bits_1 (.in_1(i), .s(s), .out_3(o));

  // Notes on the sheet:
  //   i: pull=down
  //   s: pull=down
  //   o: pull=down
endmodule
