// Logisim project From_Bottom_Up_Theories.circ as structural Verilog
module BasicBlocks_2_1 (
  input  A,
  input  A_2,
  input  A_3,
  input  B,
  input  A_4,
  input  B_2,
  input  in_7,
  input  A_5,
  input  in_9,
  input  B_3,
  input  A_6,
  input  A_7,
  input  B_4,
  input  B_5,
  input  A_8,
  input  in_16,
  input  B_6,
  input  in_18,
  input  XNOR,
  input  in_20,
  input  A_9,
  input  in_22,
  input  in_23,
  input  B_7,
  output out,
  output out_2,
  output out_3,
  output out_4,
  output out_29,
  output out_5,
  output out_6,
  output out_7,
  output out_33,
  output out_8,
  output out_35,
  output out_36,
  output out_37
);

  wire and_2_out, and_3_out, and_5_out, and_6_out, not_5_out, not_6_out, or_2_out, or_3_out, or_4_out,
       transistor_1_out, transistor_2_out, transistor_3_out, transistor_4_out, transistor_6_out,
       transistor_7_out, transistor_8_out, transistor_10_out, transistor_11_out, transistor_12_out,
       transistor_14_out, transistor_16_out, transistor_17_out, transistor_18_out, transistor_19_out,
       transistor_21_out, transistor_23_out, transistor_24_out, transistor_25_out, transistor_26_out,
       undriven, undriven_2, undriven_3, undriven_4, undriven_5, undriven_6, undriven_7, undriven_8,
       undriven_9, undriven_10, undriven_11, undriven_12, undriven_13, undriven_14, undriven_15, undriven_16,
       undriven_17, undriven_18, undriven_19, undriven_20, undriven_21, undriven_22, undriven_23,
       undriven_24, undriven_25, xor_2_out;

  buf buffer_1 (out, A);
  not not_1 (out_2, A_2);
  or or_1 (out_4, A_4, B_2);
  nor nor_1 (out_29, in_7, in_9);
  xor xor_1 (out_33, in_16, in_18);
  and and_1 (out_3, A_3, B);
  nand nand_1 (out_6, A_6, B_4);
  xnor xnor_1 (out_35, XNOR, in_22);
  Transistor transistor_1 (.in(undriven_6), .out(transistor_1_out), .gate(undriven_3));
  Transistor transistor_2 (.out(transistor_2_out), .gate(undriven_4));  // open: in
  Transistor transistor_3 (.in(transistor_2_out), .out(transistor_3_out), .gate(undriven_5));
  Transistor transistor_4 (.in(undriven_7), .out(transistor_4_out), .gate(undriven));
  Transistor transistor_5 (.in(undriven_7), .out(transistor_4_out), .gate(undriven_2));
  or or_2 (or_2_out, A_5, B_3);
  not not_2 (out_5, or_2_out);
  and and_2 (and_2_out, A_7, B_5);
  not not_3 (out_7, and_2_out);
  xor xor_2 (xor_2_out, in_20, in_23);
  not not_4 (out_36, xor_2_out);
  and and_3 (and_3_out, A_8, B_6);
  not not_5 (not_5_out, and_3_out);
  or or_3 (or_3_out, A_8, B_6);
  Transistor transistor_6 (.out(transistor_6_out), .gate(undriven_8));  // open: in
  Transistor transistor_7 (.in(transistor_6_out), .out(transistor_7_out), .gate(undriven_9));
  Transistor transistor_8 (.in(undriven_13), .out(transistor_8_out), .gate(undriven_10));
  Transistor transistor_9 (.in(undriven_13), .out(transistor_8_out), .gate(undriven_11));
  Transistor transistor_10 (.in(undriven_12), .out(transistor_10_out), .gate(transistor_7_out));
  and and_4 (out_8, not_5_out, or_3_out);
  and and_5 (and_5_out, A_9, B_7);
  or or_4 (or_4_out, A_9, B_7);
  Transistor transistor_11 (.in(undriven_14), .out(transistor_11_out), .gate(transistor_8_out));
  not not_6 (not_6_out, and_5_out);
  Transistor transistor_12 (.in(undriven_17), .out(transistor_12_out), .gate(undriven_15));
  Transistor transistor_13 (.in(undriven_17), .out(transistor_12_out), .gate(undriven_16));
  and and_6 (and_6_out, not_6_out, or_4_out);
  Transistor transistor_14 (.in(undriven_18), .out(transistor_14_out), .gate(undriven_15));
  Transistor transistor_15 (.in(undriven_18), .out(transistor_14_out), .gate(undriven_16));
  not not_7 (out_37, and_6_out);
  Transistor transistor_16 (.in(undriven_19), .out(transistor_16_out), .gate(transistor_12_out));
  Transistor transistor_17 (.out(transistor_17_out), .gate(undriven_19));  // open: in
  Transistor transistor_18 (.in(transistor_17_out), .out(transistor_18_out), .gate(transistor_14_out));
  Transistor transistor_19 (.in(undriven_22), .out(transistor_19_out), .gate(undriven_20));
  Transistor transistor_20 (.in(undriven_22), .out(transistor_19_out), .gate(undriven_21));
  Transistor transistor_21 (.in(undriven_23), .out(transistor_21_out), .gate(undriven_20));
  Transistor transistor_22 (.in(undriven_23), .out(transistor_21_out), .gate(undriven_21));
  Transistor transistor_23 (.in(undriven_24), .out(transistor_23_out), .gate(transistor_19_out));
  Transistor transistor_24 (.out(transistor_24_out), .gate(undriven_24));  // open: in
  Transistor transistor_25 (.in(transistor_24_out), .out(transistor_25_out), .gate(transistor_21_out));
  Transistor transistor_26 (.in(undriven_25), .out(transistor_26_out), .gate(transistor_25_out));
  // also tied to GND on the sheet: {transistor_4_out, transistor_1_out, transistor_3_out, transistor_7_out, transistor_8_out, transistor_10_out, transistor_11_out, transistor_12_out, transistor_16_out, transistor_14_out, transistor_18_out, transistor_19_out, transistor_23_out, transistor_21_out, transistor_25_out, transistor_26_out}

  // Notes on the sheet:
  //   Buffer
  //   NOT
  //   AND
  //   OR
  //   NOR
  //   NAND
  //   XOR
  //   A
  //   A
  //   A
  //   B
  //   out
  //   B
  //   out
  //   out
  //   out
  //   A
  //   B
  //   A
  //   B
  //   out
  //   A
  //   B
  //   A
  //   B
  //   out
  //   out
endmodule

module ICS_QUAD_2_1 (
  input  in_1,
  input  in_2,
  input  in_3,
  input  in_4,
  input  in_5,
  input  in_6,
  input  in_7,
  input  in_8,
  input  in_9,
  input  in_10,
  input  in_11,
  input  in_12,
  input  in_13,
  input  in_14,
  input  in_15,
  input  in_16,
  input  in_17,
  input  in_18,
  input  in_19,
  input  in_20,
  input  in_21,
  output out_22,
  output out_23,
  output out_24,
  output out_25,
  output out_26,
  output out_27,
  output out_28,
  output out_29,
  output out_30,
  output out_31,
  output out_32
);

  wire and_1_out, and_2_out, and_3_out, and_4_out, nand_quad_2_1_vcc_1_out_14;

  nand nand_1 (out_22, in_2, in_1);
  nand nand_2 (out_28, in_15, in_14);
  NAND_QUAD_2_1 nand_quad_2_1_1 (
    .in_1(in_1), .in_2(in_2), .in_5(in_3), .in_6(in_6), .out_9(out_22), .out_11(out_23));  // open: in_3, in_4, in_7, in_8, out_10, out_12
  nand nand_3 (out_26, in_10, in_13);
  nand nand_4 (out_29, in_16, in_17);
  and and_1 (and_1_out, in_7, in_4, in_5);
  xor xor_1 (out_24, and_1_out, in_5);
  and and_2 (and_2_out, in_20, in_18, in_5);
  xor xor_2 (out_30, and_2_out, in_5);
  // NoConnect on 1'b0
  xor xor_3 (out_27, in_5, and_4_out);
  and and_3 (and_3_out, in_5, in_19, in_21);
  xor xor_4 (out_31, in_5, and_3_out);
  NAND_QUAD_2_1_VCC nand_quad_2_1_vcc_1 (
    .in_1(in_5), .in_6(in_8), .in_8(in_9), .in_2(in_4), .in_4(in_7), .out_14(nand_quad_2_1_vcc_1_out_14),
    .out_10(out_24), .out_12(out_25));  // open: in_7, in_9, in_3, in_5, out_13, out_11
  and and_4 (and_4_out, in_5, in_11, in_12);

  assign out_32 = 1'b0;
  // also tied to GND on the sheet: nand_quad_2_1_vcc_1_out_14

  // Other names for the same wires on the sheet: A1 = in_1; A1_1 = in_4; B1 = in_2; B1_1 = in_7; VCC = in_5;
  //   Y1 = out_22; Y1_1 = out_24

  // Notes on the sheet:
  //   7400
  //   NAND_QUAD_2_1
  //   Tobuild up from transistor is not poassibleTransitors are broken, we need to just simulate it's behaviour
endmodule

module NAND_QUAD_2_1_VCC (
  input  in_1,
  input  in_2,
  input  in_3,
  input  in_4,
  input  in_5,
  input  in_6,
  input  in_7,
  input  in_8,
  input  in_9,
  output out_10,
  output out_11,
  output out_12,
  output out_13,
  output out_14
);

  wire and_1_out, and_2_out, and_3_out, and_4_out;

  and and_1 (and_1_out, in_4, in_2, in_1);
  xor xor_1 (out_10, and_1_out, in_1);
  and and_2 (and_2_out, in_8, in_6, in_1);
  xor xor_2 (out_12, and_2_out, in_1);
  // NoConnect on 1'b0
  xor xor_3 (out_13, in_1, and_4_out);
  and and_3 (and_3_out, in_1, in_3, in_5);
  xor xor_4 (out_11, in_1, and_3_out);
  and and_4 (and_4_out, in_1, in_7, in_9);

  assign out_14 = 1'b0;
endmodule

module NAND_QUAD_2_1 (
  input  in_1,
  input  in_2,
  input  in_3,
  input  in_4,
  input  in_5,
  input  in_6,
  input  in_7,
  input  in_8,
  output out_9,
  output out_10,
  output out_11,
  output out_12
);

  nand nand_1 (out_9, in_2, in_1);
  nand nand_2 (out_11, in_6, in_5);
  nand nand_3 (out_10, in_3, in_4);
  nand nand_4 (out_12, in_7, in_8);
endmodule

module EN_DIS_CONTROL (
  input  in_1,
  output out_2
);

  wire clock_1_out;

  Clock clock_1 (.out(clock_1_out));
  and and_1 (out_2, clock_1_out, in_1);
endmodule

module WAVE_FORM_GEN (
);

  wire clock_1_out;

  Clock clock_1 (.out(clock_1_out));

  // Notes on the sheet:
  //   JOHNSON SHIFT COUNTER
endmodule

module SR_LATCH (
  input  in_1,
  input  in_2,
  output out_3,
  output out_4
);

  nor nor_1 (out_3, in_1, out_4);
  nor nor_2 (out_4, out_3, in_2);
endmodule

module BasicBlocks_Latches (
  input  in_1,
  input  in_2,
  input  in_3,
  input  in_4,
  input  in_5,
  input  in_6,
  input  in_7,
  output out_8,
  output out_9,
  output out_10,
  output out_11,
  output out_12,
  output out_13,
  output out_14,
  output out_15
);

  wire or_2_out, or_3_out, or_4_out;

  or or_1 (out_8, in_1, out_8);
  nor nor_1 (out_11, in_6, out_12);
  nor nor_2 (out_12, out_11, in_7);
  SR_LATCH sr_latch_1 (.in_2(in_7), .in_1(in_6), .out_4(out_15), .out_3(out_14));
  or or_2 (or_2_out, in_2, in_3);
  not not_1 (out_9, or_2_out);
  or or_3 (or_3_out, in_4, out_13);
  or or_4 (or_4_out, out_10, in_5);
  not not_2 (out_10, or_3_out);
  not not_3 (out_13, or_4_out);

  // Other names for the same wires on the sheet: R = in_6; S = in_7

  // Notes on the sheet:
  //   SR LATCH
endmodule
